// Logisim project cpu21-riscv.circ as structural Verilog: 17 circuits, main circuit ◇理想流水线
module \单周期RISC_V  (
  input  IR1,
  input  IR2,
  input  IR3,
  output RegWrite,
  output MemWrite,
  output [31:0] PC,
  output [31:0] IR,
  output [31:0] RDin,
  output [31:0] MDin,
  output [31:0] LedData
);

  wire ALT, alu_1_equal, alu_1_out_4, and_1_out, and_2_out, and_3_out, and_4_out, and_5_out, and_7_out, Bge,
       CLK, clock_1_out, comparator_1_eq, comparator_2_eq, comparator_2_lt, controlled_buffer_1_out,
       d_ff_1_q, ecall, Go, go_halt, halt, IR1_t, IR2_t, IR3_t, IRA, IRB, IRC, JAL, JALR, MTR, nand_1_out,
       not_1_out, not_2_out, not_3_out, not_4_out, not_5_out, not_6_out, or_1_out, or_5_out, PCSrc,
       riscv_probe_1_p2, RST, sb, SType, W1, W2, W3, \单周期硬布线控制器_1_alu_src , \单周期硬布线控制器_1_beq ,
       \单周期硬布线控制器_1_bne ;
  wire [3:0] MemSel, shifter_3_out, \单周期硬布线控制器_1_alu_op ;
  wire [4:0] multiplexer_3_out, multiplexer_4_out, multiplexer_9_out;
  wire [11:0] multiplexer_5_out;
  wire [12:0] CNT_num;
  wire [15:0] adder_1_out, \总周期数 ;
  wire [19:0] bit_extender_1_out, bit_extender_4_out, multiplexer_6_out, shifter_1_out;
  wire [31:0] adder_2_out, adder_3_out, alu_1_result, alu_1_result_2, ALUO, bit_extender_2_out,
       mips_ram_1_p7, multiplexer_1_out, multiplexer_2_out, multiplexer_7_out, multiplexer_12_out, PCOffset,
       regifile_1_r1, regifile_1_r2;

  Button \u_继续运行  (.out(Go));
  Button _1 (.out(IRA));
  Button _2 (.out(IRB));
  Button _3 (.out(IRC));
  LED #(.active("true")) led_1 (.in(W1));
  LED #(.active("true")) led_2 (.in(W2));
  LED #(.active("true")) led_3 (.in(W3));
  Hex_Digit_Display hex_digit_display_1 (.value(LedData[31:28]));  // open: dp
  not not_1 (not_1_out, halt);
  Hex_Digit_Display hex_digit_display_2 (.value(LedData[23:20]));  // open: dp
  Hex_Digit_Display hex_digit_display_3 (.value(LedData[27:24]));  // open: dp
  Register #(.width(16), .trigger("rising"), .Select("low")) \u_周期  (
    .D(adder_1_out), .en(not_1_out), .Q(\总周期数 ), .clk(CLK), .clr(RST));
  or or_1 (or_1_out, Go, and_1_out);
  and and_1 (and_1_out, not_2_out, not_3_out);
  not not_2 (not_2_out, go_halt);
  Hex_Digit_Display hex_digit_display_4 (.value(LedData[15:12]));  // open: dp
  Hex_Digit_Display hex_digit_display_5 (.value(LedData[19:16]));  // open: dp
  Adder #(.width(16)) adder_1 (.a(\总周期数 ), .b(16'h1), .out(adder_1_out));  // open: cin, cout
  Register #(.width(32), .trigger("rising"), .Select("low")) u_PC (
    .D(multiplexer_1_out), .en(or_1_out), .Q(PC), .clk(CLK), .clr(RST));
  not not_3 (not_3_out, halt);
  Hex_Digit_Display hex_digit_display_6 (.value(LedData[7:4]));  // open: dp
  Hex_Digit_Display hex_digit_display_7 (.value(LedData[11:8]));  // open: dp
  // Probe on \总周期数 
  Hex_Digit_Display hex_digit_display_8 (.value(LedData[3:0]));  // open: dp
  Register #(.width(1), .trigger("rising"), .Select("low")) u_Halt (.D(go_halt), .Q(halt), .clk(CLK));  // open: en, clr
  Adder #(.width(32)) adder_2 (.a(PC), .b(32'h4), .out(adder_2_out));  // open: cin, cout
  Adder #(.width(32)) adder_3 (.a(PC), .b(PCOffset), .out(adder_3_out));  // open: cin, cout
  Multiplexer #(.select(1), .width(32), .disabled("Z"), .enable("false")) multiplexer_1 (
    .in0(adder_2_out), .in1(multiplexer_2_out), .out(multiplexer_1_out), .sel(PCSrc));
  Multiplexer #(.select(1), .width(32), .disabled("Z"), .enable("false")) multiplexer_2 (
    .in0(adder_3_out), .in1(ALUO), .out(multiplexer_2_out), .sel(JALR));
  or or_2 (IR1_t, IR1, IRA);
  ROM #(.addrWidth(10), .dataWidth(32), .Select("high")) rom_1 (.addr(PC[11:2]), .data(IR));
  or or_3 (IR2_t, IR2, IRB);
  // RiscV_Probe riscv_probe_1: pin names not known; wires that end beside it: IR, riscv_probe_1_p2
  or or_4 (IR3_t, IR3, IRC);
  \单周期硬布线控制器  \u_单周期硬布线控制器_1  (
    .Funct({IR[30], IR[25], IR[14:12]}), .OP(IR[6:2]), .ALU_OP(\单周期硬布线控制器_1_alu_op ), .MemToReg(MTR),
    .MemWrite(MemWrite), .ALU_SRC(\单周期硬布线控制器_1_alu_src ), .RegWrite(RegWrite), .ecall(ecall), .S_type(SType),
    .Jalr(JALR), .Beq(\单周期硬布线控制器_1_beq ), .JAL(JAL), .Bne(\单周期硬布线控制器_1_bne ), .IR(IR[21]),
    .uret(riscv_probe_1_p2), .Bge(Bge), .sb(sb), .ALT(ALT));  // open: RsUsed, RtUsed, IRE, IRD
  Multiplexer #(.select(1), .width(5), .disabled("Z"), .enable("false")) multiplexer_3 (
    .in0(IR[19:15]), .in1(5'b01010), .out(multiplexer_3_out), .sel(ecall));
  Multiplexer #(.select(1), .width(5), .disabled("Z"), .enable("false")) multiplexer_4 (
    .in0(IR[24:20]), .in1(5'b10001), .out(multiplexer_4_out), .sel(ecall));
  Multiplexer #(.select(1), .width(12), .disabled("Z"), .enable("false")) multiplexer_5 (
    .in0(IR[31:20]), .in1({IR[31:25], IR[11:7]}), .out(multiplexer_5_out), .sel(SType));
  assign bit_extender_1_out = {{8{IR[31]}}, {IR[31], IR[7], IR[30:25], IR[11:8]}};  // Bit_Extender bit_extender_1
  assign bit_extender_2_out = {{20{multiplexer_5_out[11]}}, multiplexer_5_out};  // Bit_Extender bit_extender_2
  Multiplexer #(.select(1), .width(20), .disabled("Z"), .enable("false")) multiplexer_6 (
    .in0(bit_extender_1_out), .in1({IR[31], IR[19:12], IR[20], IR[30:21]}), .out(multiplexer_6_out), .sel(JAL));
  Regifile regifile_1 (
    .Din(RDin), .Clk(CLK), .R1(regifile_1_r1), .R2(regifile_1_r2), .WE(RegWrite), .W_num(IR[11:7]),
    .R1_num(multiplexer_3_out), .R2_num(multiplexer_4_out));
  Multiplexer #(.select(1), .width(32), .disabled("Z"), .enable("false")) multiplexer_7 (
    .in0(regifile_1_r2), .in1(bit_extender_2_out), .out(multiplexer_7_out), .sel(\单周期硬布线控制器_1_alu_src ));
  Multiplexer #(.select(1), .width(32), .disabled("Z"), .enable("false")) multiplexer_8 (
    .in0(multiplexer_12_out), .in1(adder_2_out), .out(RDin), .sel(or_5_out));
  or or_5 (or_5_out, JALR, JAL);
  ALU alu_1 (
    .X(regifile_1_r1), .Y(multiplexer_7_out), .AluOP(\单周期硬布线控制器_1_alu_op ), .Equal(alu_1_equal),
    .Result(alu_1_result), .Result_2(alu_1_result_2), .out_4(alu_1_out_4));  // open: out_6
  Shifter #(.width(20), .shift("ll")) shifter_1 (.in(multiplexer_6_out), .\dist (5'b00001), .out(shifter_1_out));
  not not_4 (not_4_out, alu_1_equal);
  Comparator #(.width(32), .mode("twosComplement")) comparator_1 (
    .a(regifile_1_r2), .b(32'h22), .eq(comparator_1_eq));  // open: gt, lt
  Multiplexer #(.select(2), .width(5), .disabled("Z"), .enable("false")) multiplexer_9 (
    .in0({5{1'b0}}), .in1(5'b01000), .in2(5'b10000), .in3(5'b11000), .out(multiplexer_9_out),
    .sel(alu_1_result[1:0]));
  assign PCOffset = {{12{shifter_1_out[19]}}, shifter_1_out};  // Bit_Extender bit_extender_3
  D_Flip_Flop #(.trigger("high"), .Pre_Clr_Positions("LEGACY"), .NegatePresetClear("false"), .enable("true"), .NewFFLayout("false")) d_ff_1 (.Q(d_ff_1_q));  // open: clk, D, Qn, preset, en, reset
  // Probe on 13'h12
  and and_2 (and_2_out, alu_1_out_4, Bge);
  and and_3 (and_3_out, \单周期硬布线控制器_1_beq , alu_1_equal);
  and and_4 (and_4_out, \单周期硬布线控制器_1_bne , not_4_out);
  and and_5 (and_5_out, ecall, comparator_1_eq);
  and and_6 (go_halt, ecall, not_5_out);
  not not_5 (not_5_out, comparator_1_eq);
  Multiplexer #(.select(1), .width(32), .disabled("Z"), .enable("false")) multiplexer_10 (
    .in0(alu_1_result), .in1(alu_1_result_2), .out(ALUO), .sel(ALT));
  Shifter #(.width(32), .shift("ll")) shifter_2 (.in(regifile_1_r2), .\dist (multiplexer_9_out), .out(MDin));
  Comparator #(.width(13), .mode("twosComplement")) comparator_2 (
    .a(CNT_num), .b(13'h12), .eq(comparator_2_eq), .lt(comparator_2_lt));  // open: gt
  Clock #(.highDuration(1), .lowDuration(1)) clock_1 (.out(clock_1_out));
  or or_6 (PCSrc, and_4_out, and_3_out, and_2_out, JAL, JALR);
  Register #(.width(32), .trigger("rising"), .Select("low")) LED_Register (
    .D(regifile_1_r1), .en(and_5_out), .Q(LedData), .clk(CLK), .clr(RST));
  nand nand_1 (nand_1_out, d_ff_1_q, comparator_2_eq);
  Counter #(.width(13), .max('h1fff), .ongoal("stay"), .trigger("rising"), .behavior("old")) counter_1 (
    .count(comparator_2_lt), .Q(CNT_num), .clk(clock_1_out));  // open: load, D, carry, clr, preset
  Shifter #(.width(4), .shift("ll")) shifter_3 (.in(4'b0001), .\dist (alu_1_result[1:0]), .out(shifter_3_out));
  Multiplexer #(.select(1), .width(4), .disabled("Z"), .enable("false")) multiplexer_11 (
    .in0(4'b1111), .in1(shifter_3_out), .out(MemSel), .sel(sb));
  assign controlled_buffer_1_out = nand_1_out ? clock_1_out : 1'bz;  // Controlled_Buffer controlled_buffer_1
  Pull_Resistor #(.pull(1)) pull_resistor_1 (.node(controlled_buffer_1_out));
  not not_6 (not_6_out, halt);
  not not_7 (CLK, and_7_out);
  and and_7 (and_7_out, controlled_buffer_1_out, not_6_out);
  Bit_Extender #(.in_width(30), .out_width(20), .\type ("zero")) bit_extender_4 (
    .in(alu_1_result[31:2]), .out(bit_extender_4_out));
  // MIPS_RAM mips_ram_1: pin names not known; wires that end beside it: bit_extender_4_out, MDin, MemWrite, MemSel, CLK, RST, mips_ram_1_p7
  Multiplexer #(.select(1), .width(32), .disabled("Z"), .enable("false")) multiplexer_12 (
    .in0(ALUO), .in1(mips_ram_1_p7), .out(multiplexer_12_out), .sel(MTR));

  // Notes on the sheet:
  //   中断源
  //   中断等待指示
  //   数码管输出应该用寄存器锁存，否则显示数据只能一闪而过
  //   数码管输出
  //   指令存储器
  //   指令探针
  //   contents of rom_1 (hex, n*v repeats v):
  //   100493 100006f 100493 200913 300993 100006f 100493 200913 300993 100006f 100493 200913 300993
  //   100006f 100493 200913 300993 394000ef 100413 100493 1f49493 900533 2200893 73 24d493 48463 fedff06f
  //   900533 2200893 73 100493 249493 900533 2200893 73 48463 fedff06f 100493 1f49493 900533 2200893 73
  //   4034d493 900533 2200893 73 4044d493 900533 2200893 73 4044d493 900533 2200893 73 4044d493 900533
  //   2200893 73 4044d493 900533 2200893 73 4044d493 900533 2200893 73 4044d493 900533 2200893 73 4044d493
  //   900533 2200893 73 100413 1f41993 41f9d993 433 c00913 300b13 140413 f47413 800293 100313 499993
  //   89e9b3 1300533 2200893 73 406282b3 fe0294e3 140413 f00f93 1f47433 1c41413 800293 100313 49d993
  //   89e9b3 1300533 2200893 73 406282b3 fe0294e3 1c45413 406b0b33 b0463 f95ff06f 2b3 fff2c293 829293
  //   ff2e293 500533 2200893 73 fff00413 493 84a023 140413 448493 84a023 140413 448493 84a023 140413
  //   448493 84a023 140413 448493 84a023 140413 448493 84a023 140413 448493 84a023 140413 448493 84a023
  //   140413 448493 84a023 140413 448493 84a023 140413 448493 84a023 140413 448493 84a023 140413 448493
  //   84a023 140413 448493 84a023 140413 448493 84a023 140413 448493 84a023 140413 448493 140413 433
  //   3c00493 42983 4aa03 149a2b3 28663 134a023 1442023 ffc48493 fe9412e3 800533 2200893 73 440413 3c00493
  //   fc9416e3 200293 1100493 849493 1148493 1049493 900533 2200893 73 1c00e13 254d4b3 900533 2200893 73
  //   fffe0e13 fe0e16e3 a00893 73 8800493 849493 4848493 8700913 891913 5490913 2997933 1091913 11096913
  //   1200533 2200893 73 a00893 73 313 2000e13 493 100913 930023 900533 2200893 73 12484b3 130313 fffe0e13
  //   fe0e12e3 800e13 313 32483 900533 2200893 73 430313 fffe0e13 fe0e14e3 a00893 73 f00493 900533 2200893
  //   73 fff48493 fe04d8e3 a00893 73 a00893 73 413 140413 800533 2200893 73 240413 800533 2200893 73
  //   340413 800533 2200893 73 440413 800533 2200893 73 540413 800533 2200893 73 640413 800533 2200893 73
  //   740413 800533 2200893 73 840413 800533 2200893 2200893 73 8067
  //   指令字
  //   JAL
  //   JALR
  //   URET
  //   Bge
  //   BEQ offset
  //   JAL offset
  //   Beq
  //   Bne
  //   AluOP
  //   AluSrcB
  //   RegWrite
  //   S_Type
  //   ecall
  //   MemToReg
  //   MemWrite
  //   rd
  //   为方便自动评测，需要输出PC，IR，寄存器堆写如数据RDin
  //   RAM写使能MemWrite、RAM写入数据MDin等信号
  //   Bne Judge
  //   控制位
  //   暂停节拍，不能为0
  //   Bge Judge
  //   Beq Judge
  //   戳工具置1进入计数暂停模式，ctrl+k时钟自动运行到对应节拍暂停
  //   ctrl+k关闭时钟连续运行，将控制位置零，进入单步调试模式调试
  //   用这个时钟源需要去掉电路中的其他时钟源
  //   可计数暂停的时钟源
endmodule

// 单周期硬布线控制器
module \单周期硬布线控制器  (
  input  [4:0] OP,
  input  [4:0] Funct,
  input  IR,
  output [3:0] ALU_OP,
  output uret,
  output MemToReg,
  output ecall,
  output MemWrite,
  output ALU_SRC,
  output RegWrite,
  output S_type,
  output Beq,
  output Bne,
  output Jalr,
  output JAL,
  output Bge,
  output sb,
  output ALT,
  output RsUsed,
  output IRE,
  output RtUsed,
  output IRD
);

  wire \控制信号自动生成_1_ecall ;

  \运算控制器自动生成  \u_运算控制器自动生成_1  (
    .OP2(OP[0]), .OP3(OP[1]), .OP4(OP[2]), .OP5(OP[3]), .OP6(OP[4]), .F12(Funct[0]), .F13(Funct[1]),
    .F14(Funct[2]), .F25(Funct[3]), .F30(Funct[4]), .S0(ALU_OP[0]), .S1(ALU_OP[1]), .S2(ALU_OP[2]),
    .S3(ALU_OP[3]));
  \控制信号自动生成  \u_控制信号自动生成_1  (
    .OP2(OP[0]), .OP3(OP[1]), .MemToReg(MemToReg), .OP4(OP[2]), .OP5(OP[3]), .OP6(OP[4]), .F12(Funct[0]),
    .MemWrite(MemWrite), .F13(Funct[1]), .F14(Funct[2]), .F25(Funct[3]), .F30(Funct[4]), .ALU_SRC(ALU_SRC),
    .RegWrite(RegWrite), .ecall(\控制信号自动生成_1_ecall ), .S_Type(S_type), .BEQ(Beq), .BNE(Bne), .JALR(Jalr),
    .JAL(JAL), .BGE(Bge), .SB(sb), .ALT(ALT), .RsUsed(RsUsed), .RtUsed(RtUsed), .IRE(IRE), .IRD(IRD));
  and and_1 (uret, IR, \控制信号自动生成_1_ecall );
  and and_2 (ecall, ~IR, \控制信号自动生成_1_ecall );  // AND_Gate

  // Other names for the same wires on the sheet: IR21 = IR; OP_CODE[4:0] = OP

  // Notes on the sheet:
  //   运算器控制器，根据指令生成运算器功能选择信号
  //   控制信号生成，产生数据通路需要的其他控制信号
endmodule

// 运算器控制器
module \运算控制器自动生成  (
  input  OP2,
  input  OP3,
  input  OP4,
  input  OP5,
  input  OP6,
  input  F12,
  input  F13,
  input  F14,
  input  F25,
  input  F30,
  output S0,
  output S1,
  output S2,
  output S3
);

  wire and_1_out, and_2_out, and_3_out, and_4_out, and_5_out, and_6_out, and_7_out, and_8_out, and_9_out,
       and_10_out, and_11_out, and_12_out, and_13_out, and_14_out, and_15_out, and_16_out, and_17_out,
       and_18_out, and_19_out, and_20_out, and_21_out, and_22_out, and_23_out, and_24_out, and_25_out,
       and_26_out, and_27_out, and_28_out, and_29_out, and_30_out, and_31_out, and_32_out, and_33_out,
       and_34_out, and_35_out, and_36_out, and_37_out, not_1_out, not_2_out, not_3_out, not_4_out, not_5_out,
       not_6_out, not_7_out, not_8_out, not_9_out, not_10_out, not_11_out, not_12_out, not_13_out,
       not_14_out, not_15_out, not_16_out, not_17_out, not_18_out, not_19_out, not_20_out, not_21_out,
       not_22_out, not_23_out, not_24_out, not_25_out, not_26_out, not_27_out, not_28_out, not_29_out,
       not_30_out, not_31_out, not_32_out, not_33_out, not_34_out, not_35_out, not_36_out, not_37_out,
       not_38_out, not_39_out, not_40_out, not_41_out, not_42_out, not_43_out, not_44_out, not_45_out,
       not_46_out, not_47_out, not_48_out, not_49_out, not_50_out, not_51_out, not_52_out, not_53_out,
       not_54_out, not_55_out, not_56_out, not_57_out, not_58_out, not_59_out, not_60_out, not_61_out,
       not_62_out, not_63_out, not_64_out, not_65_out, not_66_out, not_67_out, not_68_out, not_69_out,
       not_70_out, not_71_out, not_72_out, not_73_out, not_74_out, not_75_out, not_76_out, not_77_out,
       not_78_out, not_79_out, not_80_out, not_81_out, not_82_out, not_83_out, not_84_out, not_85_out,
       not_86_out, not_87_out, not_88_out, not_89_out, not_90_out, not_91_out, not_92_out, not_93_out,
       not_94_out, not_95_out, not_96_out, not_97_out, not_98_out, not_99_out, not_100_out, not_101_out,
       not_102_out, not_103_out, not_104_out, not_105_out, not_106_out, not_107_out, not_108_out,
       not_109_out, not_110_out, not_111_out, not_112_out, not_113_out, not_114_out, not_115_out,
       not_116_out, not_117_out, not_118_out, not_119_out, not_120_out, not_121_out, not_122_out,
       not_123_out, not_124_out, not_125_out, not_126_out, not_127_out, not_128_out, not_129_out,
       not_130_out, not_131_out, not_132_out, not_133_out, not_134_out, not_135_out, not_136_out,
       not_137_out, not_138_out, not_139_out, not_140_out, not_141_out, not_142_out, not_143_out,
       not_144_out, not_145_out, not_146_out, not_147_out, not_148_out, not_149_out, not_150_out,
       not_151_out, not_152_out, not_153_out, not_154_out, not_155_out, not_156_out, not_157_out,
       not_158_out, not_159_out, not_160_out, not_161_out, not_162_out, not_163_out, not_164_out,
       not_165_out, not_166_out, not_167_out, not_168_out, not_169_out, not_170_out, not_171_out,
       not_172_out, not_173_out, not_174_out, not_175_out, not_176_out, not_177_out, not_178_out,
       not_179_out, not_180_out, not_181_out, not_182_out, not_183_out, not_184_out, not_185_out,
       not_186_out, not_187_out, not_188_out, not_189_out, not_190_out, not_191_out, not_192_out,
       not_193_out, not_194_out, not_195_out, not_196_out, not_197_out, not_198_out, not_199_out,
       not_200_out, not_201_out, not_202_out, not_203_out, not_204_out, not_205_out, not_206_out,
       not_207_out, not_208_out, not_209_out, not_210_out, not_211_out, not_212_out, not_213_out,
       not_214_out, not_215_out, not_216_out, not_217_out, not_218_out, not_219_out;

  not not_1 (not_1_out, F30);
  not not_2 (not_2_out, F25);
  not not_3 (not_3_out, F14);
  not not_4 (not_4_out, F13);
  not not_5 (not_5_out, F12);
  not not_6 (not_6_out, OP6);
  not not_7 (not_7_out, OP3);
  not not_8 (not_8_out, OP2);
  not not_9 (not_9_out, F30);
  not not_10 (not_10_out, F25);
  not not_11 (not_11_out, OP6);
  not not_12 (not_12_out, OP3);
  not not_13 (not_13_out, OP2);
  not not_14 (not_14_out, F30);
  not not_15 (not_15_out, F25);
  not not_16 (not_16_out, F14);
  not not_17 (not_17_out, F12);
  not not_18 (not_18_out, OP6);
  not not_19 (not_19_out, OP3);
  not not_20 (not_20_out, OP2);
  not not_21 (not_21_out, F14);
  not not_22 (not_22_out, F13);
  not not_23 (not_23_out, F12);
  not not_24 (not_24_out, OP6);
  not not_25 (not_25_out, OP5);
  not not_26 (not_26_out, OP3);
  not not_27 (not_27_out, OP2);
  not not_28 (not_28_out, OP6);
  not not_29 (not_29_out, OP5);
  not not_30 (not_30_out, OP3);
  not not_31 (not_31_out, OP2);
  not not_32 (not_32_out, F13);
  not not_33 (not_33_out, F12);
  not not_34 (not_34_out, OP6);
  not not_35 (not_35_out, OP5);
  not not_36 (not_36_out, OP3);
  not not_37 (not_37_out, OP2);
  not not_38 (not_38_out, F14);
  not not_39 (not_39_out, F12);
  not not_40 (not_40_out, OP6);
  not not_41 (not_41_out, OP5);
  not not_42 (not_42_out, OP3);
  not not_43 (not_43_out, OP2);
  not not_44 (not_44_out, F25);
  not not_45 (not_45_out, F13);
  not not_46 (not_46_out, OP6);
  not not_47 (not_47_out, OP5);
  not not_48 (not_48_out, OP3);
  not not_49 (not_49_out, OP2);
  not not_50 (not_50_out, F14);
  not not_51 (not_51_out, F12);
  not not_52 (not_52_out, OP6);
  not not_53 (not_53_out, OP5);
  not not_54 (not_54_out, OP4);
  not not_55 (not_55_out, OP3);
  not not_56 (not_56_out, OP2);
  not not_57 (not_57_out, F14);
  not not_58 (not_58_out, F12);
  not not_59 (not_59_out, OP6);
  not not_60 (not_60_out, OP4);
  not not_61 (not_61_out, OP3);
  not not_62 (not_62_out, OP2);
  not not_63 (not_63_out, F14);
  not not_64 (not_64_out, F13);
  not not_65 (not_65_out, F12);
  not not_66 (not_66_out, OP6);
  not not_67 (not_67_out, OP4);
  not not_68 (not_68_out, OP3);
  not not_69 (not_69_out, OP2);
  not not_70 (not_70_out, F13);
  not not_71 (not_71_out, OP4);
  not not_72 (not_72_out, OP3);
  not not_73 (not_73_out, OP2);
  not not_74 (not_74_out, F25);
  not not_75 (not_75_out, F14);
  not not_76 (not_76_out, F13);
  not not_77 (not_77_out, F12);
  not not_78 (not_78_out, OP6);
  not not_79 (not_79_out, OP3);
  not not_80 (not_80_out, OP2);
  not not_81 (not_81_out, F30);
  not not_82 (not_82_out, F25);
  not not_83 (not_83_out, OP6);
  not not_84 (not_84_out, OP3);
  not not_85 (not_85_out, OP2);
  not not_86 (not_86_out, F30);
  not not_87 (not_87_out, F25);
  not not_88 (not_88_out, F14);
  not not_89 (not_89_out, F12);
  not not_90 (not_90_out, OP6);
  not not_91 (not_91_out, OP3);
  not not_92 (not_92_out, OP2);
  not not_93 (not_93_out, OP6);
  not not_94 (not_94_out, OP5);
  not not_95 (not_95_out, OP3);
  not not_96 (not_96_out, OP2);
  not not_97 (not_97_out, F14);
  not not_98 (not_98_out, F12);
  not not_99 (not_99_out, OP6);
  not not_100 (not_100_out, OP5);
  not not_101 (not_101_out, OP3);
  not not_102 (not_102_out, OP2);
  not not_103 (not_103_out, F30);
  not not_104 (not_104_out, F25);
  not not_105 (not_105_out, F13);
  not not_106 (not_106_out, OP6);
  not not_107 (not_107_out, OP5);
  not not_108 (not_108_out, OP3);
  not not_109 (not_109_out, OP2);
  not not_110 (not_110_out, F13);
  not not_111 (not_111_out, OP4);
  not not_112 (not_112_out, OP3);
  not not_113 (not_113_out, OP2);
  not not_114 (not_114_out, F30);
  not not_115 (not_115_out, F25);
  not not_116 (not_116_out, F14);
  not not_117 (not_117_out, F13);
  not not_118 (not_118_out, F12);
  not not_119 (not_119_out, OP6);
  not not_120 (not_120_out, OP3);
  not not_121 (not_121_out, OP2);
  not not_122 (not_122_out, F25);
  not not_123 (not_123_out, F14);
  not not_124 (not_124_out, F13);
  not not_125 (not_125_out, F12);
  not not_126 (not_126_out, OP6);
  not not_127 (not_127_out, OP3);
  not not_128 (not_128_out, OP2);
  not not_129 (not_129_out, F30);
  not not_130 (not_130_out, F25);
  not not_131 (not_131_out, OP6);
  not not_132 (not_132_out, OP3);
  not not_133 (not_133_out, OP2);
  not not_134 (not_134_out, F30);
  not not_135 (not_135_out, F25);
  not not_136 (not_136_out, F14);
  not not_137 (not_137_out, OP6);
  not not_138 (not_138_out, OP3);
  not not_139 (not_139_out, OP2);
  not not_140 (not_140_out, F14);
  not not_141 (not_141_out, F13);
  not not_142 (not_142_out, F12);
  not not_143 (not_143_out, OP6);
  not not_144 (not_144_out, OP5);
  not not_145 (not_145_out, OP3);
  not not_146 (not_146_out, OP2);
  not not_147 (not_147_out, OP6);
  not not_148 (not_148_out, OP5);
  not not_149 (not_149_out, OP3);
  not not_150 (not_150_out, OP2);
  not not_151 (not_151_out, F14);
  not not_152 (not_152_out, F12);
  not not_153 (not_153_out, OP6);
  not not_154 (not_154_out, OP5);
  not not_155 (not_155_out, OP4);
  not not_156 (not_156_out, OP3);
  not not_157 (not_157_out, OP2);
  not not_158 (not_158_out, F14);
  not not_159 (not_159_out, F12);
  not not_160 (not_160_out, OP6);
  not not_161 (not_161_out, OP4);
  not not_162 (not_162_out, OP3);
  not not_163 (not_163_out, OP2);
  not not_164 (not_164_out, F30);
  not not_165 (not_165_out, F13);
  not not_166 (not_166_out, OP6);
  not not_167 (not_167_out, OP3);
  not not_168 (not_168_out, OP2);
  not not_169 (not_169_out, F30);
  not not_170 (not_170_out, OP6);
  not not_171 (not_171_out, OP3);
  not not_172 (not_172_out, OP2);
  not not_173 (not_173_out, F14);
  not not_174 (not_174_out, F13);
  not not_175 (not_175_out, F12);
  not not_176 (not_176_out, OP6);
  not not_177 (not_177_out, OP4);
  not not_178 (not_178_out, OP3);
  not not_179 (not_179_out, OP2);
  not not_180 (not_180_out, F30);
  not not_181 (not_181_out, F25);
  not not_182 (not_182_out, F12);
  not not_183 (not_183_out, OP6);
  not not_184 (not_184_out, OP3);
  not not_185 (not_185_out, OP2);
  not not_186 (not_186_out, F30);
  not not_187 (not_187_out, F25);
  not not_188 (not_188_out, F14);
  not not_189 (not_189_out, F12);
  not not_190 (not_190_out, OP6);
  not not_191 (not_191_out, OP3);
  not not_192 (not_192_out, OP2);
  not not_193 (not_193_out, F30);
  not not_194 (not_194_out, F25);
  not not_195 (not_195_out, F14);
  not not_196 (not_196_out, OP6);
  not not_197 (not_197_out, OP3);
  not not_198 (not_198_out, OP2);
  not not_199 (not_199_out, F12);
  not not_200 (not_200_out, OP6);
  not not_201 (not_201_out, OP5);
  not not_202 (not_202_out, OP3);
  not not_203 (not_203_out, OP2);
  not not_204 (not_204_out, F13);
  not not_205 (not_205_out, F12);
  not not_206 (not_206_out, OP6);
  not not_207 (not_207_out, OP5);
  not not_208 (not_208_out, OP3);
  not not_209 (not_209_out, OP2);
  not not_210 (not_210_out, F14);
  not not_211 (not_211_out, F12);
  not not_212 (not_212_out, OP6);
  not not_213 (not_213_out, OP5);
  not not_214 (not_214_out, OP3);
  not not_215 (not_215_out, OP2);
  not not_216 (not_216_out, F13);
  not not_217 (not_217_out, OP4);
  not not_218 (not_218_out, OP3);
  not not_219 (not_219_out, OP2);
  and and_1 (and_1_out, not_1_out, not_2_out, not_3_out, not_4_out, not_5_out, not_6_out, OP5, OP4, not_7_out, not_8_out);
  and and_2 (and_2_out, not_9_out, not_10_out, F14, F13, F12, not_11_out, OP5, OP4, not_12_out, not_13_out);
  and and_3 (and_3_out, not_14_out, not_15_out, not_16_out, F13, not_17_out, not_18_out, OP5, OP4, not_19_out, not_20_out);
  and and_4 (and_4_out, not_21_out, not_22_out, not_23_out, not_24_out, not_25_out, OP4, not_26_out, not_27_out);
  and and_5 (and_5_out, F14, F13, F12, not_28_out, not_29_out, OP4, not_30_out, not_31_out);
  and and_6 (and_6_out, F14, not_32_out, not_33_out, not_34_out, not_35_out, OP4, not_36_out, not_37_out);
  and and_7 (and_7_out, not_38_out, F13, not_39_out, not_40_out, not_41_out, OP4, not_42_out, not_43_out);
  and and_8 (and_8_out, F30, not_44_out, F14, not_45_out, F12, not_46_out, not_47_out, OP4, not_48_out, not_49_out);
  and and_9 (and_9_out, not_50_out, F13, not_51_out, not_52_out, not_53_out, not_54_out, not_55_out, not_56_out);
  and and_10 (and_10_out, not_57_out, F13, not_58_out, not_59_out, OP5, not_60_out, not_61_out, not_62_out);
  and and_11 (and_11_out, not_63_out, not_64_out, not_65_out, not_66_out, OP5, not_67_out, not_68_out, not_69_out);
  and and_12 (and_12_out, F14, not_70_out, F12, OP6, OP5, not_71_out, not_72_out, not_73_out);
  and and_13 (and_13_out, F30, not_74_out, not_75_out, not_76_out, not_77_out, not_78_out, OP5, OP4, not_79_out, not_80_out);
  and and_14 (and_14_out, not_81_out, not_82_out, F14, F13, F12, not_83_out, OP5, OP4, not_84_out, not_85_out);
  and and_15 (and_15_out, not_86_out, not_87_out, not_88_out, F13, not_89_out, not_90_out, OP5, OP4, not_91_out, not_92_out);
  and and_16 (and_16_out, F14, F13, F12, not_93_out, not_94_out, OP4, not_95_out, not_96_out);
  and and_17 (and_17_out, not_97_out, F13, not_98_out, not_99_out, not_100_out, OP4, not_101_out, not_102_out);
  and and_18 (and_18_out, not_103_out, not_104_out, F14, not_105_out, F12, not_106_out, not_107_out, OP4, not_108_out, not_109_out);
  and and_19 (and_19_out, F14, not_110_out, F12, OP6, OP5, not_111_out, not_112_out, not_113_out);
  and and_20 (and_20_out, not_114_out, not_115_out, not_116_out, not_117_out, not_118_out, not_119_out, OP5, OP4, not_120_out, not_121_out);
  and and_21 (and_21_out, F30, not_122_out, not_123_out, not_124_out, not_125_out, not_126_out, OP5, OP4, not_127_out, not_128_out);
  and and_22 (and_22_out, not_129_out, not_130_out, F14, F13, F12, not_131_out, OP5, OP4, not_132_out, not_133_out);
  and and_23 (and_23_out, not_134_out, not_135_out, not_136_out, F13, F12, not_137_out, OP5, OP4, not_138_out, not_139_out);
  and and_24 (and_24_out, not_140_out, not_141_out, not_142_out, not_143_out, not_144_out, OP4, not_145_out, not_146_out);
  and and_25 (and_25_out, F14, F13, F12, not_147_out, not_148_out, OP4, not_149_out, not_150_out);
  and and_26 (and_26_out, not_151_out, F13, not_152_out, not_153_out, not_154_out, not_155_out, not_156_out, not_157_out);
  and and_27 (and_27_out, not_158_out, F13, not_159_out, not_160_out, OP5, not_161_out, not_162_out, not_163_out);
  and and_28 (and_28_out, not_164_out, F25, F14, not_165_out, F12, not_166_out, OP5, OP4, not_167_out, not_168_out);
  and and_29 (and_29_out, not_169_out, F25, F14, F13, F12, not_170_out, OP5, OP4, not_171_out, not_172_out);
  and and_30 (and_30_out, not_173_out, not_174_out, not_175_out, not_176_out, OP5, not_177_out, not_178_out, not_179_out);
  and and_31 (and_31_out, not_180_out, not_181_out, F14, F13, not_182_out, not_183_out, OP5, OP4, not_184_out, not_185_out);
  and and_32 (and_32_out, not_186_out, not_187_out, not_188_out, F13, not_189_out, not_190_out, OP5, OP4, not_191_out, not_192_out);
  and and_33 (and_33_out, not_193_out, not_194_out, not_195_out, F13, F12, not_196_out, OP5, OP4, not_197_out, not_198_out);
  and and_34 (and_34_out, F14, F13, not_199_out, not_200_out, not_201_out, OP4, not_202_out, not_203_out);
  and and_35 (and_35_out, F14, not_204_out, not_205_out, not_206_out, not_207_out, OP4, not_208_out, not_209_out);
  and and_36 (and_36_out, not_210_out, F13, not_211_out, not_212_out, not_213_out, OP4, not_214_out, not_215_out);
  and and_37 (and_37_out, F14, not_216_out, F12, OP6, OP5, not_217_out, not_218_out, not_219_out);
  or or_1 (S0, and_1_out, and_2_out, and_3_out, and_4_out, and_5_out, and_6_out, and_7_out, and_8_out, and_9_out, and_10_out, and_11_out, and_12_out);
  or or_2 (S1, and_13_out, and_14_out, and_15_out, and_16_out, and_17_out, and_18_out, and_19_out);
  or or_3 (S2, and_20_out, and_21_out, and_22_out, and_23_out, and_24_out, and_25_out, and_26_out, and_27_out, and_28_out, and_29_out, and_30_out);
  or or_4 (S3, and_31_out, and_32_out, and_33_out, and_34_out, and_35_out, and_36_out, and_37_out);
endmodule

// 控制信号生成
module \控制信号自动生成  (
  input  OP2,
  input  OP3,
  input  OP4,
  input  OP5,
  input  OP6,
  input  F12,
  input  F13,
  input  F14,
  input  F25,
  input  F30,
  output MemToReg,
  output MemWrite,
  output ALU_SRC,
  output RegWrite,
  output ecall,
  output S_Type,
  output BEQ,
  output BNE,
  output JALR,
  output JAL,
  output BGE,
  output SB,
  output ALT,
  output RsUsed,
  output RtUsed,
  output IRE,
  output IRD
);

  wire and_3_out, and_4_out, and_5_out, and_6_out, and_7_out, and_8_out, and_9_out, and_10_out, and_11_out,
       and_12_out, and_13_out, and_14_out, and_15_out, and_16_out, and_17_out, and_18_out, and_19_out,
       and_20_out, and_21_out, and_30_out, and_31_out, and_32_out, and_33_out, and_34_out, and_35_out,
       and_36_out, and_37_out, and_38_out, and_39_out, and_40_out, and_41_out, and_42_out, and_43_out,
       and_44_out, and_45_out, and_46_out, and_47_out, and_48_out, and_49_out, not_1_out, not_2_out,
       not_3_out, not_4_out, not_5_out, not_6_out, not_7_out, not_8_out, not_9_out, not_10_out, not_11_out,
       not_12_out, not_13_out, not_14_out, not_15_out, not_16_out, not_17_out, not_18_out, not_19_out,
       not_20_out, not_21_out, not_22_out, not_23_out, not_24_out, not_25_out, not_26_out, not_27_out,
       not_28_out, not_29_out, not_30_out, not_31_out, not_32_out, not_33_out, not_34_out, not_35_out,
       not_36_out, not_37_out, not_38_out, not_39_out, not_40_out, not_41_out, not_42_out, not_43_out,
       not_44_out, not_45_out, not_46_out, not_47_out, not_48_out, not_49_out, not_50_out, not_51_out,
       not_52_out, not_53_out, not_54_out, not_55_out, not_56_out, not_57_out, not_58_out, not_59_out,
       not_60_out, not_61_out, not_62_out, not_63_out, not_64_out, not_65_out, not_66_out, not_67_out,
       not_68_out, not_69_out, not_70_out, not_71_out, not_72_out, not_73_out, not_74_out, not_75_out,
       not_76_out, not_77_out, not_78_out, not_79_out, not_80_out, not_81_out, not_82_out, not_83_out,
       not_84_out, not_85_out, not_86_out, not_87_out, not_88_out, not_89_out, not_90_out, not_91_out,
       not_92_out, not_93_out, not_94_out, not_95_out, not_96_out, not_97_out, not_98_out, not_99_out,
       not_100_out, not_101_out, not_102_out, not_103_out, not_104_out, not_105_out, not_106_out,
       not_107_out, not_108_out, not_109_out, not_110_out, not_111_out, not_112_out, not_113_out,
       not_114_out, not_115_out, not_116_out, not_117_out, not_118_out, not_119_out, not_120_out,
       not_121_out, not_122_out, not_123_out, not_124_out, not_125_out, not_126_out, not_127_out,
       not_128_out, not_129_out, not_130_out, not_131_out, not_132_out, not_133_out, not_134_out,
       not_135_out, not_136_out, not_137_out, not_138_out, not_139_out, not_140_out, not_141_out,
       not_142_out, not_143_out, not_144_out, not_145_out, not_146_out, not_147_out, not_148_out,
       not_149_out, not_150_out, not_151_out, not_152_out, not_153_out, not_154_out, not_155_out,
       not_156_out, not_157_out, not_158_out, not_159_out, not_160_out, not_161_out, not_162_out,
       not_163_out, not_164_out, not_165_out, not_166_out, not_167_out, not_168_out, not_169_out,
       not_170_out, not_171_out, not_172_out, not_173_out, not_174_out, not_175_out, not_176_out,
       not_177_out, not_178_out, not_179_out, not_180_out, not_181_out, not_182_out, not_183_out,
       not_184_out, not_185_out, not_186_out, not_187_out, not_188_out, not_189_out, not_190_out,
       not_191_out, not_192_out, not_193_out, not_194_out, not_195_out, not_196_out, not_197_out,
       not_198_out, not_199_out, not_200_out, not_201_out, not_202_out, not_203_out, not_204_out,
       not_205_out, not_206_out, not_207_out, not_208_out, not_209_out, not_210_out, not_211_out,
       not_212_out, not_213_out, not_214_out, not_215_out, not_216_out, not_217_out, not_218_out,
       not_219_out, not_220_out, not_221_out, not_222_out, not_223_out, not_224_out, not_225_out,
       not_226_out, not_227_out, not_228_out, not_229_out, not_230_out, not_231_out, not_232_out,
       not_233_out, not_234_out, not_235_out, not_236_out, not_237_out, not_238_out, not_239_out,
       not_240_out, not_241_out, not_242_out, not_243_out, not_244_out, not_245_out, not_246_out,
       not_247_out, not_248_out, not_249_out, not_250_out, not_251_out, not_252_out, not_253_out,
       not_254_out, not_255_out, not_256_out, not_257_out, not_258_out, not_259_out, not_260_out,
       not_261_out, not_262_out;

  not not_1 (not_1_out, OP2);
  not not_2 (not_2_out, OP3);
  not not_3 (not_3_out, OP4);
  not not_4 (not_4_out, OP5);
  not not_5 (not_5_out, OP6);
  not not_6 (not_6_out, F12);
  not not_7 (not_7_out, F14);
  not not_8 (not_8_out, OP2);
  not not_9 (not_9_out, OP3);
  not not_10 (not_10_out, OP4);
  not not_11 (not_11_out, OP6);
  not not_12 (not_12_out, F12);
  not not_13 (not_13_out, F14);
  not not_14 (not_14_out, OP2);
  not not_15 (not_15_out, OP3);
  not not_16 (not_16_out, OP5);
  not not_17 (not_17_out, OP6);
  not not_18 (not_18_out, F12);
  not not_19 (not_19_out, F14);
  not not_20 (not_20_out, OP2);
  not not_21 (not_21_out, OP3);
  not not_22 (not_22_out, OP4);
  not not_23 (not_23_out, OP6);
  not not_24 (not_24_out, F12);
  not not_25 (not_25_out, F14);
  not not_26 (not_26_out, OP2);
  not not_27 (not_27_out, OP3);
  not not_28 (not_28_out, OP5);
  not not_29 (not_29_out, OP6);
  not not_30 (not_30_out, F12);
  not not_31 (not_31_out, OP2);
  not not_32 (not_32_out, OP3);
  not not_33 (not_33_out, OP5);
  not not_34 (not_34_out, OP6);
  not not_35 (not_35_out, F13);
  not not_36 (not_36_out, F14);
  not not_37 (not_37_out, OP2);
  not not_38 (not_38_out, OP3);
  not not_39 (not_39_out, OP5);
  not not_40 (not_40_out, OP6);
  not not_41 (not_41_out, F13);
  not not_42 (not_42_out, F25);
  not not_43 (not_43_out, OP2);
  not not_44 (not_44_out, OP3);
  not not_45 (not_45_out, OP5);
  not not_46 (not_46_out, OP6);
  not not_47 (not_47_out, OP3);
  not not_48 (not_48_out, OP4);
  not not_49 (not_49_out, F12);
  not not_50 (not_50_out, F13);
  not not_51 (not_51_out, F14);
  not not_52 (not_52_out, OP2);
  not not_53 (not_53_out, OP3);
  not not_54 (not_54_out, OP5);
  not not_55 (not_55_out, OP6);
  not not_56 (not_56_out, F12);
  not not_57 (not_57_out, F14);
  not not_58 (not_58_out, OP2);
  not not_59 (not_59_out, OP3);
  not not_60 (not_60_out, OP5);
  not not_61 (not_61_out, OP6);
  not not_62 (not_62_out, F12);
  not not_63 (not_63_out, OP2);
  not not_64 (not_64_out, OP3);
  not not_65 (not_65_out, OP5);
  not not_66 (not_66_out, OP6);
  not not_67 (not_67_out, F13);
  not not_68 (not_68_out, F14);
  not not_69 (not_69_out, OP2);
  not not_70 (not_70_out, OP3);
  not not_71 (not_71_out, OP5);
  not not_72 (not_72_out, OP6);
  not not_73 (not_73_out, F13);
  not not_74 (not_74_out, F25);
  not not_75 (not_75_out, OP2);
  not not_76 (not_76_out, OP3);
  not not_77 (not_77_out, OP6);
  not not_78 (not_78_out, F12);
  not not_79 (not_79_out, F13);
  not not_80 (not_80_out, F14);
  not not_81 (not_81_out, F25);
  not not_82 (not_82_out, OP2);
  not not_83 (not_83_out, OP3);
  not not_84 (not_84_out, OP5);
  not not_85 (not_85_out, OP6);
  not not_86 (not_86_out, OP2);
  not not_87 (not_87_out, OP3);
  not not_88 (not_88_out, OP6);
  not not_89 (not_89_out, F25);
  not not_90 (not_90_out, F30);
  not not_91 (not_91_out, OP2);
  not not_92 (not_92_out, OP3);
  not not_93 (not_93_out, OP6);
  not not_94 (not_94_out, F30);
  not not_95 (not_95_out, OP4);
  not not_96 (not_96_out, F12);
  not not_97 (not_97_out, F13);
  not not_98 (not_98_out, F14);
  not not_99 (not_99_out, OP4);
  not not_100 (not_100_out, F30);
  not not_101 (not_101_out, F25);
  not not_102 (not_102_out, F14);
  not not_103 (not_103_out, F13);
  not not_104 (not_104_out, F12);
  not not_105 (not_105_out, OP3);
  not not_106 (not_106_out, OP2);
  not not_107 (not_107_out, F30);
  not not_108 (not_108_out, F25);
  not not_109 (not_109_out, F14);
  not not_110 (not_110_out, F13);
  not not_111 (not_111_out, F12);
  not not_112 (not_112_out, OP3);
  not not_113 (not_113_out, OP2);
  not not_114 (not_114_out, OP2);
  not not_115 (not_115_out, OP3);
  not not_116 (not_116_out, OP4);
  not not_117 (not_117_out, OP6);
  not not_118 (not_118_out, F12);
  not not_119 (not_119_out, F14);
  not not_120 (not_120_out, OP2);
  not not_121 (not_121_out, OP3);
  not not_122 (not_122_out, OP4);
  not not_123 (not_123_out, F12);
  not not_124 (not_124_out, F13);
  not not_125 (not_125_out, F14);
  not not_126 (not_126_out, OP2);
  not not_127 (not_127_out, OP3);
  not not_128 (not_128_out, OP4);
  not not_129 (not_129_out, F13);
  not not_130 (not_130_out, F14);
  not not_131 (not_131_out, OP3);
  not not_132 (not_132_out, OP4);
  not not_133 (not_133_out, F12);
  not not_134 (not_134_out, F13);
  not not_135 (not_135_out, F14);
  not not_136 (not_136_out, OP4);
  not not_137 (not_137_out, OP2);
  not not_138 (not_138_out, OP3);
  not not_139 (not_139_out, OP4);
  not not_140 (not_140_out, F13);
  not not_141 (not_141_out, OP2);
  not not_142 (not_142_out, OP3);
  not not_143 (not_143_out, OP4);
  not not_144 (not_144_out, OP6);
  not not_145 (not_145_out, F12);
  not not_146 (not_146_out, F13);
  not not_147 (not_147_out, F14);
  not not_148 (not_148_out, OP2);
  not not_149 (not_149_out, OP3);
  not not_150 (not_150_out, OP6);
  not not_151 (not_151_out, F30);
  not not_152 (not_152_out, OP2);
  not not_153 (not_153_out, OP3);
  not not_154 (not_154_out, OP4);
  not not_155 (not_155_out, OP6);
  not not_156 (not_156_out, F12);
  not not_157 (not_157_out, F14);
  not not_158 (not_158_out, OP2);
  not not_159 (not_159_out, OP3);
  not not_160 (not_160_out, OP4);
  not not_161 (not_161_out, OP6);
  not not_162 (not_162_out, F12);
  not not_163 (not_163_out, F14);
  not not_164 (not_164_out, OP2);
  not not_165 (not_165_out, OP3);
  not not_166 (not_166_out, F12);
  not not_167 (not_167_out, F13);
  not not_168 (not_168_out, F14);
  not not_169 (not_169_out, F25);
  not not_170 (not_170_out, F30);
  not not_171 (not_171_out, OP3);
  not not_172 (not_172_out, OP4);
  not not_173 (not_173_out, F12);
  not not_174 (not_174_out, F13);
  not not_175 (not_175_out, F14);
  not not_176 (not_176_out, OP2);
  not not_177 (not_177_out, OP3);
  not not_178 (not_178_out, OP4);
  not not_179 (not_179_out, F13);
  not not_180 (not_180_out, OP2);
  not not_181 (not_181_out, OP3);
  not not_182 (not_182_out, OP5);
  not not_183 (not_183_out, OP6);
  not not_184 (not_184_out, F12);
  not not_185 (not_185_out, OP2);
  not not_186 (not_186_out, OP3);
  not not_187 (not_187_out, OP5);
  not not_188 (not_188_out, OP6);
  not not_189 (not_189_out, F13);
  not not_190 (not_190_out, F14);
  not not_191 (not_191_out, OP2);
  not not_192 (not_192_out, OP3);
  not not_193 (not_193_out, OP5);
  not not_194 (not_194_out, OP6);
  not not_195 (not_195_out, F13);
  not not_196 (not_196_out, F25);
  not not_197 (not_197_out, OP2);
  not not_198 (not_198_out, OP3);
  not not_199 (not_199_out, OP6);
  not not_200 (not_200_out, F12);
  not not_201 (not_201_out, F13);
  not not_202 (not_202_out, F14);
  not not_203 (not_203_out, F25);
  not not_204 (not_204_out, OP2);
  not not_205 (not_205_out, OP3);
  not not_206 (not_206_out, OP5);
  not not_207 (not_207_out, OP6);
  not not_208 (not_208_out, OP2);
  not not_209 (not_209_out, OP3);
  not not_210 (not_210_out, OP6);
  not not_211 (not_211_out, F25);
  not not_212 (not_212_out, F30);
  not not_213 (not_213_out, OP2);
  not not_214 (not_214_out, OP3);
  not not_215 (not_215_out, OP6);
  not not_216 (not_216_out, F30);
  not not_217 (not_217_out, OP2);
  not not_218 (not_218_out, OP3);
  not not_219 (not_219_out, OP2);
  not not_220 (not_220_out, OP3);
  not not_221 (not_221_out, OP4);
  not not_222 (not_222_out, OP6);
  not not_223 (not_223_out, F12);
  not not_224 (not_224_out, F14);
  not not_225 (not_225_out, OP2);
  not not_226 (not_226_out, OP3);
  not not_227 (not_227_out, OP4);
  not not_228 (not_228_out, F12);
  not not_229 (not_229_out, F13);
  not not_230 (not_230_out, F14);
  not not_231 (not_231_out, OP2);
  not not_232 (not_232_out, OP3);
  not not_233 (not_233_out, OP6);
  not not_234 (not_234_out, F12);
  not not_235 (not_235_out, F13);
  not not_236 (not_236_out, F14);
  not not_237 (not_237_out, F25);
  not not_238 (not_238_out, OP2);
  not not_239 (not_239_out, OP3);
  not not_240 (not_240_out, F12);
  not not_241 (not_241_out, F13);
  not not_242 (not_242_out, F14);
  not not_243 (not_243_out, F25);
  not not_244 (not_244_out, F30);
  not not_245 (not_245_out, OP2);
  not not_246 (not_246_out, OP3);
  not not_247 (not_247_out, OP4);
  not not_248 (not_248_out, F13);
  not not_249 (not_249_out, OP2);
  not not_250 (not_250_out, OP3);
  not not_251 (not_251_out, OP6);
  not not_252 (not_252_out, F25);
  not not_253 (not_253_out, F30);
  not not_254 (not_254_out, OP2);
  not not_255 (not_255_out, OP3);
  not not_256 (not_256_out, OP6);
  not not_257 (not_257_out, F30);
  not not_258 (not_258_out, OP2);
  not not_259 (not_259_out, OP3);
  not not_260 (not_260_out, F12);
  not not_261 (not_261_out, OP2);
  not not_262 (not_262_out, OP3);
  and and_1 (MemToReg, not_1_out, not_2_out, not_3_out, not_4_out, not_5_out, not_6_out, F13, not_7_out);
  and and_2 (MemWrite, not_8_out, not_9_out, not_10_out, OP5, not_11_out, not_12_out, not_13_out);
  and and_3 (and_3_out, not_14_out, not_15_out, not_16_out, not_17_out, not_18_out, F13, not_19_out);
  and and_4 (and_4_out, not_20_out, not_21_out, not_22_out, OP5, not_23_out, not_24_out, not_25_out);
  and and_5 (and_5_out, not_26_out, not_27_out, OP4, not_28_out, not_29_out, not_30_out);
  and and_6 (and_6_out, not_31_out, not_32_out, OP4, not_33_out, not_34_out, not_35_out, not_36_out);
  and and_7 (and_7_out, not_37_out, not_38_out, OP4, not_39_out, not_40_out, not_41_out, not_42_out);
  and and_8 (and_8_out, not_43_out, not_44_out, OP4, not_45_out, not_46_out, F13, F14);
  and and_9 (and_9_out, OP2, not_47_out, not_48_out, OP5, OP6, not_49_out, not_50_out, not_51_out);
  and and_10 (and_10_out, not_52_out, not_53_out, not_54_out, not_55_out, not_56_out, F13, not_57_out);
  and and_11 (and_11_out, not_58_out, not_59_out, OP4, not_60_out, not_61_out, not_62_out);
  and and_12 (and_12_out, not_63_out, not_64_out, OP4, not_65_out, not_66_out, not_67_out, not_68_out);
  and and_13 (and_13_out, not_69_out, not_70_out, OP4, not_71_out, not_72_out, not_73_out, not_74_out);
  and and_14 (and_14_out, not_75_out, not_76_out, OP4, not_77_out, not_78_out, not_79_out, not_80_out, not_81_out);
  and and_15 (and_15_out, not_82_out, not_83_out, OP4, not_84_out, not_85_out, F13, F14);
  and and_16 (and_16_out, not_86_out, not_87_out, OP4, OP5, not_88_out, F13, not_89_out, not_90_out);
  and and_17 (and_17_out, not_91_out, not_92_out, OP4, OP5, not_93_out, F12, F14, F25, not_94_out);
  and and_18 (and_18_out, OP2, not_95_out, OP5, OP6, not_96_out, not_97_out, not_98_out);
  and and_19 (and_19_out, OP2, OP3, not_99_out, OP5, OP6);
  and and_20 (and_20_out, not_100_out, not_101_out, not_102_out, not_103_out, not_104_out, OP6, OP5, OP4, not_105_out, not_106_out);
  and and_21 (and_21_out, not_107_out, not_108_out, not_109_out, not_110_out, not_111_out, OP6, OP5, OP4, not_112_out, not_113_out);
  and and_22 (S_Type, not_114_out, not_115_out, not_116_out, OP5, not_117_out, not_118_out, not_119_out);
  and and_23 (BEQ, not_120_out, not_121_out, not_122_out, OP5, OP6, not_123_out, not_124_out, not_125_out);
  and and_24 (BNE, not_126_out, not_127_out, not_128_out, OP5, OP6, F12, not_129_out, not_130_out);
  and and_25 (JALR, OP2, not_131_out, not_132_out, OP5, OP6, not_133_out, not_134_out, not_135_out);
  and and_26 (JAL, OP2, OP3, not_136_out, OP5, OP6);
  and and_27 (BGE, not_137_out, not_138_out, not_139_out, OP5, OP6, F12, not_140_out, F14);
  and and_28 (SB, not_141_out, not_142_out, not_143_out, OP5, not_144_out, not_145_out, not_146_out, not_147_out);
  and and_29 (ALT, not_148_out, not_149_out, OP4, OP5, not_150_out, F12, F13, F14, F25, not_151_out);
  and and_30 (and_30_out, not_152_out, not_153_out, not_154_out, not_155_out, not_156_out, F13, not_157_out);
  and and_31 (and_31_out, not_158_out, not_159_out, not_160_out, OP5, not_161_out, not_162_out, not_163_out);
  and and_32 (and_32_out, not_164_out, not_165_out, OP5, not_166_out, not_167_out, not_168_out, not_169_out, not_170_out);
  and and_33 (and_33_out, not_171_out, not_172_out, OP5, OP6, not_173_out, not_174_out, not_175_out);
  and and_34 (and_34_out, not_176_out, not_177_out, not_178_out, OP5, OP6, F12, not_179_out);
  and and_35 (and_35_out, not_180_out, not_181_out, OP4, not_182_out, not_183_out, not_184_out);
  and and_36 (and_36_out, not_185_out, not_186_out, OP4, not_187_out, not_188_out, not_189_out, not_190_out);
  and and_37 (and_37_out, not_191_out, not_192_out, OP4, not_193_out, not_194_out, not_195_out, not_196_out);
  and and_38 (and_38_out, not_197_out, not_198_out, OP4, not_199_out, not_200_out, not_201_out, not_202_out, not_203_out);
  and and_39 (and_39_out, not_204_out, not_205_out, OP4, not_206_out, not_207_out, F13, F14);
  and and_40 (and_40_out, not_208_out, not_209_out, OP4, OP5, not_210_out, F13, not_211_out, not_212_out);
  and and_41 (and_41_out, not_213_out, not_214_out, OP4, OP5, not_215_out, F12, F14, F25, not_216_out);
  and and_42 (and_42_out, not_217_out, not_218_out, OP4, OP5, OP6, F13, F14);
  and and_43 (and_43_out, not_219_out, not_220_out, not_221_out, OP5, not_222_out, not_223_out, not_224_out);
  and and_44 (and_44_out, not_225_out, not_226_out, not_227_out, OP5, not_228_out, not_229_out, not_230_out);
  and and_45 (and_45_out, not_231_out, not_232_out, OP5, not_233_out, not_234_out, not_235_out, not_236_out, not_237_out);
  and and_46 (and_46_out, not_238_out, not_239_out, OP5, not_240_out, not_241_out, not_242_out, not_243_out, not_244_out);
  and and_47 (and_47_out, not_245_out, not_246_out, not_247_out, OP5, OP6, F12, not_248_out);
  and and_48 (and_48_out, not_249_out, not_250_out, OP4, OP5, not_251_out, F13, not_252_out, not_253_out);
  and and_49 (and_49_out, not_254_out, not_255_out, OP4, OP5, not_256_out, F12, F14, F25, not_257_out);
  and and_50 (IRE, not_258_out, not_259_out, OP4, OP5, OP6, not_260_out, F13, F14);
  and and_51 (IRD, not_261_out, not_262_out, OP4, OP5, OP6, F12, F13, F14);
  or or_1 (ALU_SRC, and_3_out, and_4_out, and_5_out, and_6_out, and_7_out, and_8_out, and_9_out);
  or or_2 (ecall, and_20_out, and_21_out);
  or or_3 (RtUsed, and_43_out, and_44_out, and_45_out, and_46_out, and_47_out, and_48_out, and_49_out);
  or or_4 (RegWrite, and_10_out, and_11_out, and_12_out, and_13_out, and_14_out, and_15_out, and_16_out, and_17_out, and_18_out, and_19_out);
  or or_5 (RsUsed, and_30_out, and_31_out, and_32_out, and_33_out, and_34_out, and_35_out, and_36_out, and_37_out, and_38_out, and_39_out, and_40_out, and_41_out, and_42_out);
endmodule

// ALU
module ALU (
  input  [31:0] X,
  input  [31:0] Y,
  input  [3:0] AluOP,
  output out_4,
  output Equal,
  output out_6,
  output [31:0] Result,
  output [31:0] Result_2
);

  wire [0:0] comparator_1_lt, comparator_2_lt;
  wire [31:0] adder_1_out, AND_out, divider_1_out, divider_1_rem, multiplier_1_cout, multiplier_1_out,
       NOR_out, OR_out, shifter_1_out, shifter_2_out, shifter_3_out, subtractor_1_out, XOR_out;

  assign AND_out = X & Y;  // AND_Gate AND, 32 bits wide
  assign OR_out = X | Y;  // OR_Gate OR, 32 bits wide
  Shifter #(.width(32), .shift("ll")) shifter_1 (.in(X), .\dist (Y[4:0]), .out(shifter_1_out));
  Shifter #(.width(32), .shift("ar")) shifter_2 (.in(X), .\dist (Y[4:0]), .out(shifter_2_out));
  Shifter #(.width(32), .shift("lr")) shifter_3 (.in(X), .\dist (Y[4:0]), .out(shifter_3_out));
  Multiplier #(.width(32)) multiplier_1 (.a(X), .b(Y), .out(multiplier_1_out), .cout(multiplier_1_cout));  // open: cin
  Divider #(.width(32)) divider_1 (.a(X), .b(Y), .out(divider_1_out), .rem(divider_1_rem));  // open: upper
  Adder #(.width(32)) adder_1 (.a(X), .b(Y), .out(adder_1_out));  // open: cin, cout
  Subtractor #(.width(32)) subtractor_1 (.a(X), .b(Y), .out(subtractor_1_out));  // open: bin, bout
  assign XOR_out = X ^ Y;  // XOR_Gate XOR, 32 bits wide
  assign NOR_out = ~(X | Y);  // NOR_Gate NOR, 32 bits wide
  Comparator #(.width(32), .mode("twosComplement")) comparator_1 (
    .a(X), .b(Y), .eq(Equal), .lt(comparator_1_lt[0]));  // open: gt
  Comparator #(.width(32), .mode("unsigned")) comparator_2 (.a(X), .b(Y), .lt(comparator_2_lt[0]));  // open: gt, eq
  Multiplexer #(.select(4), .width(32), .disabled("Z"), .enable("false")) multiplexer_1 (
    .in0(shifter_1_out), .in1(shifter_2_out), .in2(shifter_3_out), .in3(multiplier_1_out),
    .in4(divider_1_out), .in5(adder_1_out), .in6(subtractor_1_out), .in7(AND_out), .in8(OR_out),
    .in9(XOR_out), .in10(NOR_out), .in11({{31{1'b0}}, comparator_1_lt[0]}),
    .in12({{31{1'b0}}, comparator_2_lt[0]}), .in13({32{1'b0}}), .in14({32{1'b0}}), .in15({32{1'b0}}),
    .out(Result), .sel(AluOP));
  Multiplexer #(.select(4), .width(32), .disabled("Z"), .enable("false")) multiplexer_2 (
    .in0({32{1'b0}}), .in1({32{1'b0}}), .in2({32{1'b0}}), .in3(multiplier_1_cout), .in4(divider_1_rem),
    .in5({32{1'b0}}), .in6({32{1'b0}}), .in7({32{1'b0}}), .in8({32{1'b0}}), .in9({32{1'b0}}),
    .in10({32{1'b0}}), .in11({32{1'b0}}), .in12({32{1'b0}}), .in13({32{1'b0}}), .in14({32{1'b0}}),
    .in15({32{1'b0}}), .out(Result_2), .sel(AluOP));
  Multiplexer #(.select(4), .width(1), .disabled("Z"), .enable("false")) multiplexer_3 (
    .in0(1'b0), .in1(1'b0), .in2(1'b0), .in3(1'b0), .in4(1'b0), .in5(1'b0), .in6(1'b0), .in7(1'b0),
    .in8(1'b0), .in9(1'b0), .in10(1'b0), .in11(comparator_1_lt[0]), .in12(comparator_2_lt[0]), .in13(1'b0),
    .in14(1'b0), .in15(1'b0), .out(out_6), .sel(AluOP));
  not not_1 (out_4, out_6);

  // Other names for the same wires on the sheet: Result2[31:0] = Result_2; S[3:0] = AluOP; tunnel = out_6;
  //   tunnel_t = out_4

  // Notes on the sheet:
  //   不要改变此引脚区域内容，也不要改变ALU封装形式
  //   输入引脚
  //   输出引脚
endmodule

module Regifile (
  input  [31:0] Din,
  input  Clk,
  input  WE,
  input  [4:0] R1_num,
  input  [4:0] W_num,
  input  [4:0] R2_num,
  output [31:0] R1,
  output [31:0] R2
);

  // RegisterFile registerfile_1: pin names not known; wires that end beside it: Din, Clk, WE, W_num, R1_num, R2_num, R1, R2
endmodule

module \理想流水线  (
  output RegWrite,
  output MemWrite,
  output [31:0] IF_PC,
  output [31:0] ID_PC,
  output [31:0] EX_PC,
  output [31:0] M_PC,
  output [31:0] WB_PC,
  output [31:0] RDin,
  output [31:0] MDin,
  output [31:0] LedData
);

  wire ALT, alu_1_equal, alu_1_out_4, and_1_out, and_2_out, and_3_out, and_4_out, and_5_out, and_6_out, Bge,
       clock_1_out, comparator_1_eq, comparator_2_eq, comparator_2_lt, controlled_buffer_1_out, d_ff_1_q,
       ecall, EX_MEM_out3, EX_MEM_out5, EX_MEM_out7, flow_register_bit_1_out1, flow_register_bit_1_out2,
       flow_register_bit_1_out3, flow_register_bit_1_out4, flow_register_bit_1_out5,
       flow_register_bit_1_out7, Flush, Go, go_halt, halt, IR1, IR2, IR3, JAL, JALR, MTR, nand_1_out,
       not_1_out, not_2_out, not_3_out, not_4_out, not_5_out, not_6_out, not_7_out, or_3_out, RST, sb, SType,
       W1, W2, W3, \单周期硬布线控制器_1_alt , \单周期硬布线控制器_1_alu_src , \单周期硬布线控制器_1_beq , \单周期硬布线控制器_1_bge ,
       \单周期硬布线控制器_1_bne , \单周期硬布线控制器_1_ecall , \单周期硬布线控制器_1_jal , \单周期硬布线控制器_1_jalr , \单周期硬布线控制器_1_memtoreg ,
       \单周期硬布线控制器_1_memwrite , \单周期硬布线控制器_1_regwrite , \单周期硬布线控制器_1_sb , \单周期硬布线控制器_1_uret ;
  wire [1:0] flow_register_2_outcor;
  wire [3:0] flow_register_bit_1_aluopout, MemSel, shifter_3_out, \单周期硬布线控制器_1_alu_op ;
  wire [4:0] flow_register_1_outrd, flow_register_2_outrd, multiplexer_3_out, multiplexer_4_out,
       multiplexer_8_out, WBAddr;
  wire [11:0] multiplexer_5_out;
  wire [12:0] CNT_num;
  wire [15:0] adder_1_out, \LoadUse次数 , \总周期数 , \插入气泡数 , \无条件分支数 , \条件分支成功数 ;
  wire [19:0] bit_extender_2_out, bit_extender_5_out, multiplexer_6_out;
  wire [31:0] adder_2_out, adder_3_out, adder_4_out, alu_1_result, alu_1_result_2, ALUO, bit_extender_1_out,
       bit_extender_3_out, bit_extender_4_out, CLK, EX_IR, flow_register_1_out1, flow_register_1_out2,
       flow_register_1_out3, flow_register_1_out4, flow_register_2_out1, flow_register_2_out4,
       flow_register_3_out3, ID_IR, IF_IR, MEM_IR, mips_ram_1_p7, multiplexer_1_out, multiplexer_2_out,
       multiplexer_7_out, multiplexer_9_out, PCOffset, regifile_1_r1, regifile_1_r2, shifter_2_out, WB_IR;

  Button \u_总复位  (.out(RST));
  Button _1 (.out(IR1));
  Button _2 (.out(IR2));
  Button _3 (.out(IR3));
  Button \u_继续运行  (.out(Go));
  LED #(.active("true")) led_1 (.in(W1));
  LED #(.active("true")) led_2 (.in(W2));
  LED #(.active("true")) led_3 (.in(W3));
  not not_1 (not_1_out, halt);
  Hex_Digit_Display hex_digit_display_1 (.value(LedData[31:28]));  // open: dp
  Register #(.width(16), .trigger("rising"), .Select("low")) \u_周期  (
    .D(adder_1_out), .en(not_1_out), .Q(\总周期数 ), .clk(CLK[0]), .clr(RST));
  not not_2 (not_2_out, go_halt);
  Hex_Digit_Display hex_digit_display_2 (.value(LedData[23:20]));  // open: dp
  Hex_Digit_Display hex_digit_display_3 (.value(LedData[27:24]));  // open: dp
  // OR_Gate or_1 has open pins: in0=Go, in1=and_1_out, out=open
  and and_1 (and_1_out, not_2_out, not_3_out);
  not not_3 (not_3_out, halt);
  Hex_Digit_Display hex_digit_display_4 (.value(LedData[15:12]));  // open: dp
  Hex_Digit_Display hex_digit_display_5 (.value(LedData[19:16]));  // open: dp
  Adder #(.width(16)) adder_1 (.a(\总周期数 ), .b(16'h1), .out(adder_1_out));  // open: cin, cout
  Register #(.width(32), .trigger("rising"), .Select("low")) PC (
    .D(multiplexer_2_out), .Q(IF_PC), .clk(CLK[0]), .clr(RST));  // open: en
  Hex_Digit_Display hex_digit_display_6 (.value(LedData[11:8]));  // open: dp
  Hex_Digit_Display hex_digit_display_7 (.value(LedData[7:4]));  // open: dp
  not not_4 (not_4_out, halt);
  Adder #(.width(32)) adder_2 (.a(EX_PC), .b(PCOffset), .out(adder_2_out));  // open: cin, cout
  Hex_Digit_Display hex_digit_display_8 (.value(LedData[3:0]));  // open: dp
  Register #(.width(1), .trigger("rising"), .Select("low")) u_Halt (
    .D(go_halt), .en(not_4_out), .Q(halt), .clk(CLK[0]), .clr(Go));
  Adder #(.width(32)) adder_3 (.a(IF_PC), .b(32'h4), .out(adder_3_out));  // open: cin, cout
  Multiplexer #(.select(1), .width(32), .disabled("Z"), .enable("false")) multiplexer_1 (
    .in0(adder_2_out), .in1(ALUO), .out(multiplexer_1_out), .sel(JALR));
  Multiplexer #(.select(1), .width(32), .disabled("Z"), .enable("false")) multiplexer_2 (
    .in0(adder_3_out), .in1(multiplexer_1_out), .out(multiplexer_2_out), .sel(Flush));
  // Probe on \总周期数 
  ROM #(.addrWidth(10), .dataWidth(32), .Select("high")) rom_1 (.addr(IF_PC[11:2]), .data(IF_IR));
  // Probe on \总周期数 
  // Probe on \无条件分支数 
  // Probe on \条件分支成功数 
  // Probe on \插入气泡数 
  // Probe on \LoadUse次数 
  Flow_Register IF_ID (
    .IN1(IF_IR), .Flush(Flush), .CLK(CLK[0]), .OUT1(ID_IR), .PC2(IF_PC), .PC2_2(ID_PC), .RST(RST));  // open: PC, PC_2, IN2, OUT2, IN3, OUT3, IN4, OUT4, INrd, OUTrd, INcor, OUTcor, EN, INForA, OUTForA
  // Probe on IF_PC[11:0]
  // Probe on EX_PC[11:0]
  // Probe on ID_PC[11:0]
  // Probe on M_PC[11:0]
  \单周期硬布线控制器  \u_单周期硬布线控制器_1  (
    .Funct({ID_IR[30], ID_IR[25], ID_IR[14:12]}), .OP(ID_IR[6:2]), .ALU_OP(\单周期硬布线控制器_1_alu_op ),
    .MemToReg(\单周期硬布线控制器_1_memtoreg ), .MemWrite(\单周期硬布线控制器_1_memwrite ), .ALU_SRC(\单周期硬布线控制器_1_alu_src ),
    .RegWrite(\单周期硬布线控制器_1_regwrite ), .ecall(\单周期硬布线控制器_1_ecall ), .S_type(SType),
    .Jalr(\单周期硬布线控制器_1_jalr ), .Beq(\单周期硬布线控制器_1_beq ), .JAL(\单周期硬布线控制器_1_jal ), .Bne(\单周期硬布线控制器_1_bne ),
    .IR(ID_IR[21]), .uret(\单周期硬布线控制器_1_uret ), .Bge(\单周期硬布线控制器_1_bge ), .sb(\单周期硬布线控制器_1_sb ),
    .ALT(\单周期硬布线控制器_1_alt ));  // open: RsUsed, RtUsed, IRE, IRD
  Multiplexer #(.select(1), .width(5), .disabled("Z"), .enable("false")) multiplexer_3 (
    .in0(ID_IR[19:15]), .in1(5'b01010), .out(multiplexer_3_out), .sel(\单周期硬布线控制器_1_ecall ));
  Multiplexer #(.select(1), .width(5), .disabled("Z"), .enable("false")) multiplexer_4 (
    .in0(ID_IR[24:20]), .in1(5'b10001), .out(multiplexer_4_out), .sel(\单周期硬布线控制器_1_ecall ));
  Multiplexer #(.select(1), .width(12), .disabled("Z"), .enable("false")) multiplexer_5 (
    .in0(ID_IR[31:20]), .in1({ID_IR[31:25], ID_IR[11:7]}), .out(multiplexer_5_out), .sel(SType));
  // Probe on WB_PC[11:0]
  assign bit_extender_1_out = {{20{multiplexer_5_out[11]}}, multiplexer_5_out};  // Bit_Extender bit_extender_1
  assign bit_extender_2_out = {{8{ID_IR[31]}}, {ID_IR[31], ID_IR[7], ID_IR[30:25], ID_IR[11:8]}};  // Bit_Extender bit_extender_2
  Multiplexer #(.select(1), .width(20), .disabled("Z"), .enable("false")) multiplexer_6 (
    .in0(bit_extender_2_out), .in1({ID_IR[31], ID_IR[19:12], ID_IR[20], ID_IR[30:21]}),
    .out(multiplexer_6_out), .sel(\单周期硬布线控制器_1_jal ));
  Regifile regifile_1 (
    .Din(RDin), .Clk(CLK[0]), .R1(regifile_1_r1), .R2(regifile_1_r2), .WE(RegWrite), .W_num(WBAddr),
    .R1_num(multiplexer_3_out), .R2_num(multiplexer_4_out));
  assign bit_extender_3_out = {{12{multiplexer_6_out[19]}}, multiplexer_6_out};  // Bit_Extender bit_extender_3
  Flow_Register_Bit ID_EX (
    .IN4(\单周期硬布线控制器_1_alt ), .IN3(\单周期硬布线控制器_1_jal ), .IN2(\单周期硬布线控制器_1_jalr ), .IN5(\单周期硬布线控制器_1_bge ),
    .IN6(\单周期硬布线控制器_1_sb ), .IN1(\单周期硬布线控制器_1_ecall ), .OUT4(ALT), .OUT3(JAL), .OUT2(JALR), .OUT5(Bge),
    .OUT6(sb), .OUT1(ecall), .Flush(Flush), .CLK(CLK[0]), .RST(RST));  // open: IN7, OUT7, ALUOPIN, ALUOPOut, EN
  Flow_Register_Bit flow_register_bit_1 (
    .IN4(\单周期硬布线控制器_1_beq ), .IN3(\单周期硬布线控制器_1_bne ), .IN2(\单周期硬布线控制器_1_memtoreg ),
    .IN5(\单周期硬布线控制器_1_memwrite ), .IN1(\单周期硬布线控制器_1_alu_src ), .OUT4(flow_register_bit_1_out4),
    .OUT3(flow_register_bit_1_out3), .OUT2(flow_register_bit_1_out2), .OUT5(flow_register_bit_1_out5),
    .OUT1(flow_register_bit_1_out1), .Flush(Flush), .CLK(CLK[0]), .RST(RST), .IN7(\单周期硬布线控制器_1_regwrite ),
    .OUT7(flow_register_bit_1_out7), .ALUOPIN(\单周期硬布线控制器_1_alu_op ), .ALUOPOut(flow_register_bit_1_aluopout));  // open: IN6, OUT6, EN
  Flow_Register flow_register_1 (
    .IN1(regifile_1_r1), .Flush(Flush), .CLK(CLK[0]), .OUT1(flow_register_1_out1), .PC2(ID_PC),
    .PC2_2(EX_PC), .RST(RST), .IN2(regifile_1_r2), .OUT2(flow_register_1_out2), .IN3(bit_extender_3_out),
    .OUT3(flow_register_1_out3), .IN4(bit_extender_1_out), .OUT4(flow_register_1_out4), .INrd(ID_IR[11:7]),
    .OUTrd(flow_register_1_outrd));  // open: PC, PC_2, INcor, OUTcor, EN, INForA, OUTForA
  Multiplexer #(.select(1), .width(32), .disabled("Z"), .enable("false")) multiplexer_7 (
    .in0(flow_register_1_out2), .in1(flow_register_1_out4), .out(multiplexer_7_out),
    .sel(flow_register_bit_1_out1));
  // Probe on \总周期数 
  // Probe on \总周期数 
  ALU alu_1 (
    .X(flow_register_1_out1), .Y(multiplexer_7_out), .AluOP(flow_register_bit_1_aluopout),
    .Equal(alu_1_equal), .Result(alu_1_result), .Result_2(alu_1_result_2), .out_4(alu_1_out_4));  // open: out_6
  Shifter #(.width(32), .shift("ll")) shifter_1 (.in(flow_register_1_out3), .\dist (5'b00001), .out(PCOffset));
  // Probe on IF_PC[19:0]
  // RiscV_Probe riscv_probe_1: pin names not known; wires that end beside it: IF_IR
  not not_5 (not_5_out, alu_1_equal);
  Multiplexer #(.select(2), .width(5), .disabled("Z"), .enable("false")) multiplexer_8 (
    .in0({5{1'b0}}), .in1(5'b01000), .in2(5'b10000), .in3(5'b11000), .out(multiplexer_8_out),
    .sel(alu_1_result[1:0]));
  and and_2 (and_2_out, alu_1_out_4, Bge);
  and and_3 (and_3_out, flow_register_bit_1_out3, not_5_out);
  Comparator #(.width(32), .mode("twosComplement")) comparator_1 (
    .a(flow_register_1_out2), .b(32'h22), .eq(comparator_1_eq));  // open: gt, lt
  not not_6 (not_6_out, comparator_1_eq);
  Shifter #(.width(32), .shift("ll")) shifter_2 (
    .in(flow_register_1_out2), .\dist (multiplexer_8_out), .out(shifter_2_out));
  // Probe on ID_PC[19:0]
  // RiscV_Probe riscv_probe_2: pin names not known; wires that end beside it: ID_IR
  and and_4 (and_4_out, flow_register_bit_1_out4, alu_1_equal);
  Register #(.width(32), .trigger("rising"), .Select("low")) LED_Register (
    .D(flow_register_1_out1), .en(and_5_out), .Q(LedData), .clk(CLK[0]), .clr(RST));
  and and_5 (and_5_out, ecall, comparator_1_eq);
  and and_6 (and_6_out, ecall, not_6_out);
  Multiplexer #(.select(1), .width(32), .disabled("Z"), .enable("false")) multiplexer_9 (
    .in0(alu_1_result), .in1(alu_1_result_2), .out(multiplexer_9_out), .sel(ALT));
  or or_2 (Flush, and_3_out, and_4_out, and_2_out, JAL, JALR);
  Adder #(.width(32)) adder_4 (.a(32'h4), .b(EX_PC), .out(adder_4_out));  // open: cin, cout
  // Probe on EX_PC[19:0]
  // RiscV_Probe riscv_probe_3: pin names not known; wires that end beside it: EX_IR
  or or_3 (or_3_out, JALR, JAL);
  assign bit_extender_4_out = {{2{1'b0}}, alu_1_result[31:2]};  // Bit_Extender bit_extender_4
  Multiplexer #(.select(1), .width(32), .disabled("Z"), .enable("false")) multiplexer_10 (
    .in0(multiplexer_9_out), .in1(adder_4_out), .out(CLK), .sel(or_3_out));
  // Probe on M_PC[19:0]
  // RiscV_Probe riscv_probe_4: pin names not known; wires that end beside it: MEM_IR
  Flow_Register_Bit EX_MEM (
    .IN3(flow_register_bit_1_out7), .IN5(flow_register_bit_1_out2), .IN1(flow_register_bit_1_out5),
    .OUT3(EX_MEM_out3), .OUT5(EX_MEM_out5), .OUT1(MemWrite), .Flush(Flush), .CLK(CLK[0]), .RST(RST),
    .IN7(and_6_out), .OUT7(EX_MEM_out7));  // open: IN4, IN2, IN6, OUT4, OUT2, OUT6, ALUOPIN, ALUOPOut, EN
  Flow_Register flow_register_2 (
    .Flush(Flush), .CLK(CLK[0]), .OUT1(flow_register_2_out1), .PC2(EX_PC), .PC2_2(M_PC), .RST(RST),
    .IN3(shifter_2_out), .OUT3(MDin), .IN4(bit_extender_4_out), .OUT4(flow_register_2_out4),
    .INrd(flow_register_1_outrd), .OUTrd(flow_register_2_outrd), .INcor(alu_1_result[1:0]),
    .OUTcor(flow_register_2_outcor));  // open: IN1, PC, PC_2, IN2, OUT2, EN, INForA, OUTForA
  // RiscV_Probe riscv_probe_5: pin names not known; wires that end beside it: WB_IR
  // Probe on WB_PC[19:0]
  Bit_Extender #(.in_width(32), .out_width(20), .\type ("zero")) bit_extender_5 (
    .in(flow_register_2_out4), .out(bit_extender_5_out));
  Shifter #(.width(4), .shift("ll")) shifter_3 (.in(4'b0001), .\dist (flow_register_2_outcor), .out(shifter_3_out));
  Multiplexer #(.select(1), .width(4), .disabled("Z"), .enable("false")) multiplexer_11 (
    .in0(4'b1111), .in1(shifter_3_out), .out(MemSel), .sel(sb));
  D_Flip_Flop #(.trigger("high"), .Pre_Clr_Positions("LEGACY"), .NegatePresetClear("false"), .enable("true"), .NewFFLayout("false")) d_ff_1 (.Q(d_ff_1_q));  // open: clk, D, Qn, preset, en, reset
  // Probe on 13'h12
  // MIPS_RAM mips_ram_1: pin names not known; wires that end beside it: bit_extender_5_out, MDin, MemWrite, MemSel, CLK, RST, mips_ram_1_p7, flow_register_2_out1, mips_ram_1_p7, flow_register_2_outrd, M_PC
  Comparator #(.width(13), .mode("twosComplement")) comparator_2 (
    .a(CNT_num), .b(13'h12), .eq(comparator_2_eq), .lt(comparator_2_lt));  // open: gt
  Clock #(.highDuration(1), .lowDuration(1)) clock_1 (.out(clock_1_out));
  nand nand_1 (nand_1_out, d_ff_1_q, comparator_2_eq);
  Counter #(.width(13), .max('h1fff), .ongoal("stay"), .trigger("rising"), .behavior("old")) counter_1 (
    .count(comparator_2_lt), .Q(CNT_num), .clk(clock_1_out));  // open: load, D, carry, clr, preset
  Flow_Register_Bit MEM_WB (
    .IN3(EX_MEM_out3), .IN5(EX_MEM_out5), .OUT3(RegWrite), .OUT5(MTR), .Flush(Flush), .CLK(CLK[0]),
    .RST(RST), .IN7(EX_MEM_out7), .OUT7(go_halt));  // open: IN4, IN2, IN6, IN1, OUT4, OUT2, OUT6, OUT1, ALUOPIN, ALUOPOut, EN
  Flow_Register flow_register_3 (
    .IN1(flow_register_2_out1), .Flush(Flush), .CLK(CLK[0]), .OUT1(ALUO), .PC2(M_PC), .PC2_2(WB_PC),
    .RST(RST), .IN3(mips_ram_1_p7), .OUT3(flow_register_3_out3), .INrd(flow_register_2_outrd), .OUTrd(WBAddr));  // open: PC, PC_2, IN2, OUT2, IN4, OUT4, INcor, OUTcor, EN, INForA, OUTForA
  assign controlled_buffer_1_out = nand_1_out ? clock_1_out : 1'bz;  // Controlled_Buffer controlled_buffer_1
  Pull_Resistor #(.pull(1)) pull_resistor_1 (.node(controlled_buffer_1_out));
  Multiplexer #(.select(1), .width(32), .disabled("Z"), .enable("false")) multiplexer_12 (
    .in0(ALUO), .in1(flow_register_3_out3), .out(RDin), .sel(MTR));
  not not_7 (not_7_out, halt);
  and and_7 (CLK[0], controlled_buffer_1_out, not_7_out);
  // Pins of 1 and 32 bits meet at CLK

  // Other names for the same wires on the sheet: IR[31:0] = ID_IR; MEM_PC[31:0] = M_PC; PCSig[31:0] = EX_PC;
  //   PCSrc = Flush

  // Notes on the sheet:
  //   中断源
  //   中断等待指示
  //   数码管输出
  //   指令存储器
  //   contents of rom_1 (hex, n*v repeats v):
  //   413 493 913 993 46413 14e493 296913 39e993 842023 942223 1242423 1342623 a00893 493 913 993 73
  //   指令字
  //   JAL
  //   JALR
  //   URET
  //   Bge
  //   BEQ offset
  //   JAL offset
  //   流水调试日志用
  //   Beq
  //   Bne
  //   MemToReg
  //   MemWrite
  //   AluOP
  //   AluSrcB
  //   RegWrite
  //   S_Type
  //   ecall
  //   rd
  //   时空图监测，可删除
  //   为方便自动评测，需要输出流水线各段保存的PC值，注意是PC不是PC+4，另外ID段寄存器写入信息，Mem段内存写入信息也要输出
  //   Bne Judge
  //   Beq Judge
  //   rd
  //   Bge Judge
  //   rd
  //   控制位
  //   暂停节拍，不能为0
  //   戳工具置1进入计数暂停模式，ctrl+k时钟自动运行到对应节拍暂停
  //   ctrl+k关闭时钟连续运行，将控制位置零，进入单步调试模式调试
  //   用这个时钟源需要去掉电路中的其他时钟源
  //   可计数暂停的时钟源
endmodule

module \气泡流水线  (
  output RegWrite,
  output MemWrite,
  output [31:0] IF_PC,
  output [31:0] ID_PC,
  output [31:0] EX_PC,
  output [31:0] M_PC,
  output [31:0] WB_PC,
  output [31:0] RDin,
  output [31:0] MDin,
  output [31:0] LedData
);

  wire ALT, alu_1_equal, alu_1_out_4, and_1_out, and_3_out, and_4_out, and_5_out, and_6_out, and_7_out, Bge,
       CLK, clock_1_out, comparator_1_eq, comparator_1_lt, comparator_2_eq, controlled_buffer_1_out,
       d_ff_1_q, ecall, EX_MEM_out3, EX_MEM_out5, EX_MEM_out7, flow_register_bit_1_out1,
       flow_register_bit_1_out2, flow_register_bit_1_out3, flow_register_bit_1_out4,
       flow_register_bit_1_out5, flow_register_bit_1_out7, Flush, Go, go_halt, halt, ID_EX_out6, IR1, IR2,
       IR3, JAL, JALR, MTR, nand_1_out, not_1_out, not_2_out, not_3_out, not_4_out, not_5_out, not_6_out,
       not_7_out, or_3_out, PCSrc, RST, RsUsed, RtUsed, sb, Stall, SType, W1, W2, W3, \单周期硬布线控制器_1_alt ,
       \单周期硬布线控制器_1_alu_src , \单周期硬布线控制器_1_beq , \单周期硬布线控制器_1_bge , \单周期硬布线控制器_1_bne , \单周期硬布线控制器_1_ecall ,
       \单周期硬布线控制器_1_jal , \单周期硬布线控制器_1_jalr , \单周期硬布线控制器_1_memtoreg , \单周期硬布线控制器_1_memwrite ,
       \单周期硬布线控制器_1_regwrite , \单周期硬布线控制器_1_sb , \单周期硬布线控制器_1_uret ;
  wire [1:0] flow_register_2_outcor;
  wire [3:0] flow_register_bit_1_aluopout, MemSel, shifter_3_out, \单周期硬布线控制器_1_alu_op ;
  wire [4:0] flow_register_1_outrd, flow_register_2_outrd, multiplexer_8_out, Rs, Rt, WBAddr;
  wire [11:0] multiplexer_5_out;
  wire [12:0] CNT_num;
  wire [15:0] adder_1_out, \LoadUse次数 , \总周期数 , \插入气泡数 , \无条件分支数 , \条件分支成功数 ;
  wire [19:0] bit_extender_2_out, bit_extender_5_out, multiplexer_6_out;
  wire [31:0] adder_2_out, adder_3_out, adder_4_out, alu_1_result_2, ALUO, bit_extender_1_out,
       bit_extender_3_out, bit_extender_4_out, EX_IR, flow_register_1_out1, flow_register_1_out2,
       flow_register_1_out3, flow_register_1_out4, flow_register_2_out1, flow_register_2_out4,
       flow_register_3_out1, flow_register_3_out3, ID_IR, IF_IR, MEM_IR, mips_ram_1_p7, multiplexer_1_out,
       multiplexer_2_out, multiplexer_7_out, multiplexer_9_out, multiplexer_10_out, PCOffset, regifile_1_r1,
       regifile_1_r2, shifter_2_out, WB_IR;

  Button \u_总复位  (.out(RST));
  Button _1 (.out(IR1));
  Button _2 (.out(IR2));
  Button _3 (.out(IR3));
  // Probe on \总周期数 
  // Probe on \总周期数 
  Button \u_继续运行  (.out(Go));
  LED #(.active("true")) led_1 (.in(W1));
  LED #(.active("true")) led_2 (.in(W2));
  LED #(.active("true")) led_3 (.in(W3));
  Hex_Digit_Display hex_digit_display_1 (.value(LedData[31:28]));  // open: dp
  // Probe on IF_PC[19:0]
  // RiscV_Probe riscv_probe_1: pin names not known; wires that end beside it: IF_IR
  Hex_Digit_Display hex_digit_display_2 (.value(LedData[27:24]));  // open: dp
  Hex_Digit_Display hex_digit_display_3 (.value(LedData[23:20]));  // open: dp
  // Probe on ID_PC[19:0]
  // RiscV_Probe riscv_probe_2: pin names not known; wires that end beside it: ID_IR
  Register #(.width(16), .trigger("rising"), .Select("low")) \u_周期  (
    .D(adder_1_out), .en(not_1_out), .Q(\总周期数 ), .clk(CLK), .clr(RST));
  not not_1 (not_1_out, halt);
  not not_2 (not_2_out, go_halt);
  Hex_Digit_Display hex_digit_display_4 (.value(LedData[19:16]));  // open: dp
  Hex_Digit_Display hex_digit_display_5 (.value(LedData[15:12]));  // open: dp
  // OR_Gate or_1 has open pins: in0=Go, in1=and_1_out, out=open
  and and_1 (and_1_out, not_2_out, not_3_out);
  not not_3 (not_3_out, halt);
  Hex_Digit_Display hex_digit_display_6 (.value(LedData[11:8]));  // open: dp
  Hex_Digit_Display hex_digit_display_7 (.value(LedData[7:4]));  // open: dp
  // Probe on EX_PC[19:0]
  // RiscV_Probe riscv_probe_3: pin names not known; wires that end beside it: EX_IR
  Adder #(.width(16)) adder_1 (.a(\总周期数 ), .b(16'h1), .out(adder_1_out));  // open: cin, cout
  Register #(.width(32), .trigger("rising"), .Select("low")) PC (
    .D(multiplexer_2_out), .en(Stall), .Q(IF_PC), .clk(CLK), .clr(RST));
  Hex_Digit_Display hex_digit_display_8 (.value(LedData[3:0]));  // open: dp
  not not_4 (not_4_out, halt);
  Adder #(.width(32)) adder_2 (.a(EX_PC), .b(PCOffset), .out(adder_2_out));  // open: cin, cout
  // Probe on \总周期数 
  // Probe on M_PC[19:0]
  // RiscV_Probe riscv_probe_4: pin names not known; wires that end beside it: MEM_IR
  Register #(.width(1), .trigger("falling"), .Select("low")) u_Halt (
    .D(go_halt), .en(not_4_out), .Q(halt), .clk(CLK), .clr(Go));
  Adder #(.width(32)) adder_3 (.a(IF_PC), .b(32'h4), .out(adder_3_out));  // open: cin, cout
  Multiplexer #(.select(1), .width(32), .disabled("Z"), .enable("false")) multiplexer_1 (
    .in0(adder_2_out), .in1(ALUO), .out(multiplexer_1_out), .sel(JALR));
  Multiplexer #(.select(1), .width(32), .disabled("Z"), .enable("false")) multiplexer_2 (
    .in0(adder_3_out), .in1(multiplexer_1_out), .out(multiplexer_2_out), .sel(PCSrc));
  // Probe on \总周期数 
  // Probe on \无条件分支数 
  // Probe on \条件分支成功数 
  // Probe on \插入气泡数 
  // Probe on \LoadUse次数 
  ROM #(.addrWidth(10), .dataWidth(32), .Select("high")) rom_1 (.addr(IF_PC[11:2]), .data(IF_IR));
  Fowarding_Logic fowarding_logic_1 (
    .Ex_RegWrite(flow_register_bit_1_out7), .PCSrc(PCSrc), .Stall(Stall), .Flush(Flush),
    .MEM_RegWrite(EX_MEM_out3), .Rs(Rs), .Rt(Rt), .ExAddr(flow_register_1_outrd),
    .MEMAddr(flow_register_2_outrd), .RsUsed(RsUsed), .RtUsed(RtUsed));  // open: RsForward, RtForward, Ex_MemRead
  // Probe on IF_PC[11:0]
  // Probe on WB_PC[19:0]
  // RiscV_Probe riscv_probe_5: pin names not known; wires that end beside it: WB_IR
  // Probe on EX_PC[11:0]
  // Probe on ID_PC[11:0]
  Flow_Register IF_ID (
    .IN1(IF_IR), .Flush(Flush), .CLK(CLK), .OUT1(ID_IR), .PC2(IF_PC), .PC2_2(ID_PC), .RST(RST), .EN(Stall));  // open: PC, PC_2, IN2, OUT2, IN3, OUT3, IN4, OUT4, INrd, OUTrd, INcor, OUTcor, INForA, OUTForA
  // Probe on M_PC[11:0]
  D_Flip_Flop #(.trigger("high"), .Pre_Clr_Positions("LEGACY"), .NegatePresetClear("false"), .enable("true"), .NewFFLayout("false")) d_ff_1 (.Q(d_ff_1_q));  // open: clk, D, Qn, preset, en, reset
  // Probe on 13'h12
  // Probe on WB_PC[11:0]
  Comparator #(.width(13), .mode("twosComplement")) comparator_1 (
    .a(CNT_num), .b(13'h12), .eq(comparator_1_eq), .lt(comparator_1_lt));  // open: gt
  Clock #(.highDuration(1), .lowDuration(1)) clock_1 (.out(clock_1_out));
  \单周期硬布线控制器  \u_单周期硬布线控制器_1  (
    .Funct({ID_IR[30], ID_IR[25], ID_IR[14:12]}), .OP(ID_IR[6:2]), .ALU_OP(\单周期硬布线控制器_1_alu_op ),
    .MemToReg(\单周期硬布线控制器_1_memtoreg ), .MemWrite(\单周期硬布线控制器_1_memwrite ), .ALU_SRC(\单周期硬布线控制器_1_alu_src ),
    .RegWrite(\单周期硬布线控制器_1_regwrite ), .ecall(\单周期硬布线控制器_1_ecall ), .S_type(SType),
    .Jalr(\单周期硬布线控制器_1_jalr ), .Beq(\单周期硬布线控制器_1_beq ), .JAL(\单周期硬布线控制器_1_jal ), .Bne(\单周期硬布线控制器_1_bne ),
    .IR(ID_IR[21]), .uret(\单周期硬布线控制器_1_uret ), .Bge(\单周期硬布线控制器_1_bge ), .sb(\单周期硬布线控制器_1_sb ),
    .ALT(\单周期硬布线控制器_1_alt ), .RsUsed(RsUsed), .RtUsed(RtUsed));  // open: IRE, IRD
  Multiplexer #(.select(1), .width(5), .disabled("Z"), .enable("false")) multiplexer_3 (
    .in0(ID_IR[19:15]), .in1(5'b01010), .out(Rs), .sel(\单周期硬布线控制器_1_ecall ));
  Multiplexer #(.select(1), .width(5), .disabled("Z"), .enable("false")) multiplexer_4 (
    .in0(ID_IR[24:20]), .in1(5'b10001), .out(Rt), .sel(\单周期硬布线控制器_1_ecall ));
  Multiplexer #(.select(1), .width(12), .disabled("Z"), .enable("false")) multiplexer_5 (
    .in0(ID_IR[31:20]), .in1({ID_IR[31:25], ID_IR[11:7]}), .out(multiplexer_5_out), .sel(SType));
  nand nand_1 (nand_1_out, d_ff_1_q, comparator_1_eq);
  Counter #(.width(13), .max('h1fff), .ongoal("stay"), .trigger("rising"), .behavior("old")) counter_1 (
    .count(comparator_1_lt), .Q(CNT_num), .clk(clock_1_out));  // open: load, D, carry, clr, preset
  assign bit_extender_1_out = {{20{multiplexer_5_out[11]}}, multiplexer_5_out};  // Bit_Extender bit_extender_1
  assign bit_extender_2_out = {{8{ID_IR[31]}}, {ID_IR[31], ID_IR[7], ID_IR[30:25], ID_IR[11:8]}};  // Bit_Extender bit_extender_2
  Multiplexer #(.select(1), .width(20), .disabled("Z"), .enable("false")) multiplexer_6 (
    .in0(bit_extender_2_out), .in1({ID_IR[31], ID_IR[19:12], ID_IR[20], ID_IR[30:21]}),
    .out(multiplexer_6_out), .sel(\单周期硬布线控制器_1_jal ));
  assign controlled_buffer_1_out = nand_1_out ? clock_1_out : 1'bz;  // Controlled_Buffer controlled_buffer_1
  Regifile regifile_1 (
    .Din(RDin), .Clk(CLK), .R1(regifile_1_r1), .R2(regifile_1_r2), .WE(RegWrite), .W_num(WBAddr),
    .R1_num(Rs), .R2_num(Rt));
  Pull_Resistor #(.pull(1)) pull_resistor_1 (.node(controlled_buffer_1_out));
  assign bit_extender_3_out = {{12{multiplexer_6_out[19]}}, multiplexer_6_out};  // Bit_Extender bit_extender_3
  not not_5 (not_5_out, halt);
  Flow_Register_Bit ID_EX (
    .IN4(\单周期硬布线控制器_1_alt ), .IN3(\单周期硬布线控制器_1_jal ), .IN2(\单周期硬布线控制器_1_jalr ), .IN5(\单周期硬布线控制器_1_bge ),
    .IN6(\单周期硬布线控制器_1_sb ), .IN1(\单周期硬布线控制器_1_ecall ), .OUT4(ALT), .OUT3(JAL), .OUT2(JALR), .OUT5(Bge),
    .OUT6(ID_EX_out6), .OUT1(ecall), .Flush(Flush), .CLK(CLK), .RST(RST));  // open: IN7, OUT7, ALUOPIN, ALUOPOut, EN
  Flow_Register_Bit flow_register_bit_1 (
    .IN4(\单周期硬布线控制器_1_beq ), .IN3(\单周期硬布线控制器_1_bne ), .IN2(\单周期硬布线控制器_1_memtoreg ),
    .IN5(\单周期硬布线控制器_1_memwrite ), .IN1(\单周期硬布线控制器_1_alu_src ), .OUT4(flow_register_bit_1_out4),
    .OUT3(flow_register_bit_1_out3), .OUT2(flow_register_bit_1_out2), .OUT5(flow_register_bit_1_out5),
    .OUT1(flow_register_bit_1_out1), .Flush(Flush), .CLK(CLK), .RST(RST), .IN7(\单周期硬布线控制器_1_regwrite ),
    .OUT7(flow_register_bit_1_out7), .ALUOPIN(\单周期硬布线控制器_1_alu_op ), .ALUOPOut(flow_register_bit_1_aluopout));  // open: IN6, OUT6, EN
  Flow_Register flow_register_1 (
    .IN1(regifile_1_r1), .Flush(Flush), .CLK(CLK), .OUT1(flow_register_1_out1), .PC(ID_IR), .PC_2(EX_IR),
    .PC2(ID_PC), .PC2_2(EX_PC), .RST(RST), .IN2(regifile_1_r2), .OUT2(flow_register_1_out2),
    .IN3(bit_extender_3_out), .OUT3(flow_register_1_out3), .IN4(bit_extender_1_out),
    .OUT4(flow_register_1_out4), .INrd(ID_IR[11:7]), .OUTrd(flow_register_1_outrd));  // open: INcor, OUTcor, EN, INForA, OUTForA
  and and_2 (CLK, controlled_buffer_1_out, not_5_out);
  Multiplexer #(.select(1), .width(32), .disabled("Z"), .enable("false")) multiplexer_7 (
    .in0(flow_register_1_out2), .in1(flow_register_1_out4), .out(multiplexer_7_out),
    .sel(flow_register_bit_1_out1));
  ALU alu_1 (
    .X(flow_register_1_out1), .Y(multiplexer_7_out), .AluOP(flow_register_bit_1_aluopout),
    .Equal(alu_1_equal), .Result(ALUO), .Result_2(alu_1_result_2), .out_4(alu_1_out_4));  // open: out_6
  Shifter #(.width(32), .shift("ll")) shifter_1 (.in(flow_register_1_out3), .\dist (5'b00001), .out(PCOffset));
  and and_3 (and_3_out, flow_register_bit_1_out3, not_6_out);
  not not_6 (not_6_out, alu_1_equal);
  Comparator #(.width(32), .mode("twosComplement")) comparator_2 (
    .a(flow_register_1_out2), .b(32'h22), .eq(comparator_2_eq));  // open: gt, lt
  not not_7 (not_7_out, comparator_2_eq);
  Multiplexer #(.select(2), .width(5), .disabled("Z"), .enable("false")) multiplexer_8 (
    .in0({5{1'b0}}), .in1(5'b01000), .in2(5'b10000), .in3(5'b11000), .out(multiplexer_8_out), .sel(ALUO[1:0]));
  and and_4 (and_4_out, alu_1_out_4, Bge);
  and and_5 (and_5_out, flow_register_bit_1_out4, alu_1_equal);
  and and_6 (and_6_out, ecall, comparator_2_eq);
  and and_7 (and_7_out, ecall, not_7_out);
  Multiplexer #(.select(1), .width(32), .disabled("Z"), .enable("false")) multiplexer_9 (
    .in0(ALUO), .in1(alu_1_result_2), .out(multiplexer_9_out), .sel(ALT));
  Shifter #(.width(32), .shift("ll")) shifter_2 (
    .in(flow_register_1_out2), .\dist (multiplexer_8_out), .out(shifter_2_out));
  or or_2 (PCSrc, and_3_out, and_5_out, and_4_out, JAL, JALR);
  Register #(.width(32), .trigger("rising"), .Select("low")) LED_Register (
    .D(flow_register_1_out1), .en(and_6_out), .Q(LedData), .clk(CLK), .clr(RST));
  or or_3 (or_3_out, JALR, JAL);
  assign bit_extender_4_out = {{2{1'b0}}, ALUO[31:2]};  // Bit_Extender bit_extender_4
  Adder #(.width(32)) adder_4 (.a(32'h4), .b(EX_PC), .out(adder_4_out));  // open: cin, cout
  Multiplexer #(.select(1), .width(32), .disabled("Z"), .enable("false")) multiplexer_10 (
    .in0(multiplexer_9_out), .in1(adder_4_out), .out(multiplexer_10_out), .sel(or_3_out));
  Flow_Register_Bit EX_MEM (
    .IN3(flow_register_bit_1_out7), .IN2(ID_EX_out6), .IN5(flow_register_bit_1_out2),
    .IN1(flow_register_bit_1_out5), .OUT3(EX_MEM_out3), .OUT2(sb), .OUT5(EX_MEM_out5), .OUT1(MemWrite),
    .Flush(1'b0), .CLK(CLK), .RST(RST), .IN7(and_7_out), .OUT7(EX_MEM_out7));  // open: IN4, IN6, OUT4, OUT6, ALUOPIN, ALUOPOut, EN
  Flow_Register flow_register_2 (
    .IN1(multiplexer_10_out), .Flush(1'b0), .CLK(CLK), .OUT1(flow_register_2_out1), .PC(EX_IR),
    .PC_2(MEM_IR), .PC2(EX_PC), .PC2_2(M_PC), .RST(RST), .IN3(shifter_2_out), .OUT3(MDin),
    .IN4(bit_extender_4_out), .OUT4(flow_register_2_out4), .INrd(flow_register_1_outrd),
    .OUTrd(flow_register_2_outrd), .INcor(ALUO[1:0]), .OUTcor(flow_register_2_outcor));  // open: IN2, OUT2, EN, INForA, OUTForA
  Bit_Extender #(.in_width(32), .out_width(20), .\type ("zero")) bit_extender_5 (
    .in(flow_register_2_out4), .out(bit_extender_5_out));
  Shifter #(.width(4), .shift("ll")) shifter_3 (.in(4'b0001), .\dist (flow_register_2_outcor), .out(shifter_3_out));
  // MIPS_RAM mips_ram_1: pin names not known; wires that end beside it: bit_extender_5_out, MDin, MemWrite, MemSel, CLK, RST, mips_ram_1_p7, MEM_IR
  Multiplexer #(.select(1), .width(4), .disabled("Z"), .enable("false")) multiplexer_11 (
    .in0(4'b1111), .in1(shifter_3_out), .out(MemSel), .sel(sb));
  Flow_Register_Bit MEM_WB (
    .IN3(EX_MEM_out3), .IN5(EX_MEM_out5), .OUT3(RegWrite), .OUT5(MTR), .Flush(1'b0), .CLK(CLK), .RST(RST),
    .IN7(EX_MEM_out7), .OUT7(go_halt));  // open: IN4, IN2, IN6, IN1, OUT4, OUT2, OUT6, OUT1, ALUOPIN, ALUOPOut, EN
  Flow_Register flow_register_3 (
    .IN1(flow_register_2_out1), .Flush(1'b0), .CLK(CLK), .OUT1(flow_register_3_out1), .PC(MEM_IR),
    .PC_2(WB_IR), .PC2(M_PC), .PC2_2(WB_PC), .RST(RST), .IN3(mips_ram_1_p7), .OUT3(flow_register_3_out3),
    .INrd(flow_register_2_outrd), .OUTrd(WBAddr));  // open: IN2, OUT2, IN4, OUT4, INcor, OUTcor, EN, INForA, OUTForA
  Multiplexer #(.select(1), .width(32), .disabled("Z"), .enable("false")) multiplexer_12 (
    .in0(flow_register_3_out1), .in1(flow_register_3_out3), .out(RDin), .sel(MTR));

  // Other names for the same wires on the sheet: MEM_PC[31:0] = M_PC; PCSig[31:0] = EX_PC

  // Notes on the sheet:
  //   中断源
  //   时空图监测，可删除
  //   中断等待指示
  //   数码管输出
  //   指令存储器
  //   contents of rom_1 (hex, n*v repeats v):
  //   100493 100006f 100493 200913 300993 100006f 100493 200913 300993 100006f 100493 200913 300993
  //   100006f 100493 200913 300993 29c000ef 100413 100493 1f49493 900533 2200893 73 24d493 48463 fedff06f
  //   900533 2200893 73 100493 249493 900533 2200893 73 48463 fedff06f 100493 1f49493 900533 2200893 73
  //   4034d493 900533 2200893 73 4044d493 900533 2200893 73 4044d493 900533 2200893 73 4044d493 900533
  //   2200893 73 4044d493 900533 2200893 73 4044d493 900533 2200893 73 4044d493 900533 2200893 73 4044d493
  //   900533 2200893 73 100413 1f41993 41f9d993 433 c00913 300b13 140413 f47413 800293 100313 499993
  //   89e9b3 1300533 2200893 73 406282b3 fe0294e3 140413 f00f93 1f47433 1c41413 800293 100313 49d993
  //   89e9b3 1300533 2200893 73 406282b3 fe0294e3 1c45413 406b0b33 b0463 f95ff06f 2b3 fff2c293 829293
  //   ff2e293 500533 2200893 73 fff00413 493 84a023 140413 448493 84a023 140413 448493 84a023 140413
  //   448493 84a023 140413 448493 84a023 140413 448493 84a023 140413 448493 84a023 140413 448493 84a023
  //   140413 448493 84a023 140413 448493 84a023 140413 448493 84a023 140413 448493 84a023 140413 448493
  //   84a023 140413 448493 84a023 140413 448493 84a023 140413 448493 84a023 140413 448493 140413 433
  //   3c00493 42983 4aa03 149a2b3 28663 134a023 1442023 ffc48493 fe9412e3 800533 2200893 73 440413 3c00493
  //   fc9416e3 a00893 73 413 140413 800533 2200893 73 240413 800533 2200893 73 340413 800533 2200893 73
  //   440413 800533 2200893 73 540413 800533 2200893 73 640413 800533 2200893 73 740413 800533 2200893 73
  //   840413 800533 2200893 2200893 73 8067
  //   控制位
  //   指令字
  //   流水调试日志用
  //   暂停节拍，不能为0
  //   JAL
  //   JALR
  //   URET
  //   Bge
  //   BEQ offset
  //   JAL offset
  //   用这个时钟源需要去掉电路中的其他时钟源
  //   Beq
  //   Bne
  //   MemToReg
  //   MemWrite
  //   AluOP
  //   AluSrcB
  //   RegWrite
  //   S_Type
  //   ecall
  //   可计数暂停的时钟源
  //   rd
  //   为方便自动评测，需要输出流水线各段保存的PC值，注意是PC不是PC+4，另外ID段寄存器写入信息，Mem段内存写入信息也要输出
  //   Beq Judge
  //   Bne Judge
  //   Bge Judge
  //   rd
  //   rd
endmodule
module \重定向流水线  (
  output RegWrite,
  output MemWrite,
  output [31:0] IF_PC,
  output [31:0] ID_PC,
  output [31:0] EX_PC,
  output [31:0] M_PC,
  output [31:0] WB_PC,
  output [31:0] RDin,
  output [31:0] MDin,
  output [31:0] LedData
);

  wire ALT, alu_1_equal, alu_1_out_4, and_1_out, and_3_out, and_4_out, and_5_out, and_6_out, and_7_out,
       and_8_out, Bge, CLK, clock_1_out, comparator_1_eq, comparator_1_lt, comparator_2_eq, comparator_3_eq,
       controlled_buffer_1_out, d_ff_1_q, demultiplexer_1_out1, demultiplexer_1_out2, demultiplexer_1_out3,
       ecall, EX_MEM_out3, EX_MEM_out5, EX_MEM_out7, flow_register_bit_1_out1, flow_register_bit_1_out3,
       flow_register_bit_1_out4, flow_register_bit_1_out5, flow_register_bit_1_out7, Flush, Go, go_halt,
       halt, ID_EX_out6, IE, IR1, IR2, IR3, IRespond, JAL, JALR, MEMRead, MTR, nand_1_out, not_1_out,
       not_2_out, not_3_out, not_4_out, not_5_out, not_6_out, not_7_out, not_8_out, not_9_out, or_1_out,
       or_2_out, or_4_out, or_5_out, PCSrc, priority_encoder_1_gs, RST, RsUsed, RtUsed, sb, Stall, SType,
       URET, W1, W2, W3, \中断按键参考电路_1_iro , \中断按键参考电路_2_iro , \中断按键参考电路_3_iro , \单周期硬布线控制器_1_alt ,
       \单周期硬布线控制器_1_alu_src , \单周期硬布线控制器_1_beq , \单周期硬布线控制器_1_bge , \单周期硬布线控制器_1_bne , \单周期硬布线控制器_1_ecall ,
       \单周期硬布线控制器_1_jal , \单周期硬布线控制器_1_jalr , \单周期硬布线控制器_1_memtoreg , \单周期硬布线控制器_1_memwrite ,
       \单周期硬布线控制器_1_regwrite , \单周期硬布线控制器_1_sb ;
  wire [1:0] flow_register_1_outcor, flow_register_1_outfora, flow_register_2_outcor,
       fowarding_logic_1_rsforward, fowarding_logic_1_rtforward, IREncode, register_1_q;
  wire [3:0] flow_register_bit_1_aluopout, MemSel, shifter_3_out, \单周期硬布线控制器_1_alu_op ;
  wire [4:0] flow_register_1_outrd, flow_register_2_outrd, multiplexer_13_out, Rs, Rt, WBAddr;
  wire [11:0] multiplexer_8_out;
  wire [12:0] CNT_num;
  wire [15:0] adder_1_out, adder_4_out, adder_5_out, adder_6_out, adder_7_out, adder_8_out,
       bit_extender_1_out, bit_extender_5_out, bit_extender_6_out, bit_extender_7_out, bit_extender_8_out,
       \LoadUse次数 , \总周期数 , \插入气泡数 , \无条件分支数 , \条件分支成功数 ;
  wire [19:0] bit_extender_3_out, bit_extender_10_out, multiplexer_9_out;
  wire [31:0] adder_2_out, adder_3_out, adder_9_out, alu_1_result_2, ALUO, bit_extender_2_out,
       bit_extender_4_out, bit_extender_9_out, EX_IR, flow_register_1_out1, flow_register_1_out2,
       flow_register_1_out3, flow_register_1_out4, flow_register_2_out4, flow_register_3_out1,
       flow_register_3_out3, ForEX, IAddr, ID_IR, IF_IR, MEM_IR, mEPC_q, mips_ram_1_p7, multiplexer_1_out,
       multiplexer_2_out, multiplexer_4_out, multiplexer_5_out, multiplexer_10_out, multiplexer_11_out,
       multiplexer_12_out, multiplexer_14_out, multiplexer_15_out, PCOffset, regifile_1_r1, regifile_1_r2,
       shifter_2_out, WB_IR;

  Button \u_总复位  (.out(RST));
  Button _1 (.out(IR1));
  Button _2 (.out(IR2));
  Button _3 (.out(IR3));
  // Probe on \总周期数 
  // Probe on \总周期数 
  Button \u_继续运行  (.out(Go));
  LED #(.active("true")) led_1 (.in(W1));
  LED #(.active("true")) led_2 (.in(W2));
  LED #(.active("true")) led_3 (.in(W3));
  Hex_Digit_Display hex_digit_display_1 (.value(LedData[31:28]));  // open: dp
  // Probe on IF_PC[19:0]
  // RiscV_Probe riscv_probe_1: pin names not known; wires that end beside it: IF_IR
  Hex_Digit_Display hex_digit_display_2 (.value(LedData[23:20]));  // open: dp
  Hex_Digit_Display hex_digit_display_3 (.value(LedData[27:24]));  // open: dp
  // Probe on ID_PC[19:0]
  // RiscV_Probe riscv_probe_2: pin names not known; wires that end beside it: ID_IR
  Register #(.width(16), .trigger("rising"), .Select("low")) \u_周期  (
    .D(adder_1_out), .en(not_1_out), .Q(\总周期数 ), .clk(CLK), .clr(RST));
  not not_1 (not_1_out, halt);
  Multiplexer #(.select(1), .width(32), .disabled("Z"), .enable("false")) multiplexer_1 (
    .in0(multiplexer_5_out), .in1(IAddr), .out(multiplexer_1_out), .sel(or_1_out));
  or or_1 (or_1_out, URET, IRespond);
  Hex_Digit_Display hex_digit_display_4 (.value(LedData[19:16]));  // open: dp
  Hex_Digit_Display hex_digit_display_5 (.value(LedData[15:12]));  // open: dp
  Hex_Digit_Display hex_digit_display_6 (.value(LedData[7:4]));  // open: dp
  Hex_Digit_Display hex_digit_display_7 (.value(LedData[11:8]));  // open: dp
  // Probe on EX_PC[19:0]
  // RiscV_Probe riscv_probe_3: pin names not known; wires that end beside it: EX_IR
  Adder #(.width(16)) adder_1 (.a(\总周期数 ), .b(16'h1), .out(adder_1_out));  // open: cin, cout
  Register #(.width(32), .trigger("rising"), .Select("low")) PC (
    .D(multiplexer_1_out), .en(Stall), .Q(IF_PC), .clk(CLK), .clr(RST));
  Multiplexer #(.select(2), .width(32), .disabled("Z"), .enable("false")) multiplexer_2 (
    .in1(32'h30ac), .in2(32'h3150), .in3(32'h31f4), .out(multiplexer_2_out), .sel(IREncode));  // open: in0
  Hex_Digit_Display hex_digit_display_8 (.value(LedData[3:0]));  // open: dp
  not not_2 (not_2_out, halt);
  Adder #(.width(32)) adder_2 (.a(EX_PC), .b(PCOffset), .out(adder_2_out));  // open: cin, cout
  Register #(.width(32), .trigger("rising"), .Select("low")) mEPC (
    .D(multiplexer_5_out), .en(IRespond), .Q(mEPC_q), .clk(CLK));  // open: clr
  Multiplexer #(.select(1), .width(32), .disabled("Z"), .enable("false")) multiplexer_3 (
    .in0(multiplexer_2_out), .in1(mEPC_q), .out(IAddr), .sel(URET));
  // Probe on \总周期数 
  // Probe on M_PC[19:0]
  // RiscV_Probe riscv_probe_4: pin names not known; wires that end beside it: MEM_IR
  Register #(.width(1), .trigger("falling"), .Select("low")) u_Halt (
    .D(go_halt), .en(not_2_out), .Q(halt), .clk(CLK), .clr(Go));
  Adder #(.width(32)) adder_3 (.a(IF_PC), .b(32'h4), .out(adder_3_out));  // open: cin, cout
  Multiplexer #(.select(1), .width(32), .disabled("Z"), .enable("false")) multiplexer_4 (
    .in0(adder_2_out), .in1(ALUO), .out(multiplexer_4_out), .sel(JALR));
  Multiplexer #(.select(1), .width(32), .disabled("Z"), .enable("false")) multiplexer_5 (
    .in0(adder_3_out), .in1(multiplexer_4_out), .out(multiplexer_5_out), .sel(PCSrc));
  // Probe on \总周期数 
  // Probe on \无条件分支数 
  // Probe on \条件分支成功数 
  // Probe on \插入气泡数 
  // Probe on \LoadUse次数 
  ROM #(.addrWidth(10), .dataWidth(32), .Select("high")) rom_1 (.addr(IF_PC[11:2]), .data(IF_IR));
  Fowarding_Logic fowarding_logic_1 (
    .Ex_RegWrite(flow_register_bit_1_out7), .PCSrc(PCSrc), .Stall(Stall), .Flush(Flush),
    .MEM_RegWrite(EX_MEM_out3), .Rs(Rs), .Rt(Rt), .ExAddr(flow_register_1_outrd),
    .MEMAddr(flow_register_2_outrd), .RsUsed(RsUsed), .RtUsed(RtUsed),
    .RsForward(fowarding_logic_1_rsforward), .RtForward(fowarding_logic_1_rtforward), .Ex_MemRead(MEMRead));
  // Probe on IF_PC[11:0]
  // Probe on WB_PC[19:0]
  // RiscV_Probe riscv_probe_5: pin names not known; wires that end beside it: WB_IR
  Register #(.width(16), .trigger("rising"), .Select("low")) \u_无条件分支数  (
    .D(adder_4_out), .Q(\无条件分支数 ), .clk(CLK), .clr(RST));  // open: en
  or or_2 (or_2_out, JAL, JALR);
  // Probe on EX_PC[11:0]
  // Probe on ID_PC[11:0]
  Flow_Register IF_ID (
    .IN1(IF_IR), .Flush(PCSrc), .CLK(CLK), .OUT1(ID_IR), .PC2(IF_PC), .PC2_2(ID_PC), .RST(RST), .EN(Stall));  // open: PC, PC_2, IN2, OUT2, IN3, OUT3, IN4, OUT4, INrd, OUTrd, INcor, OUTcor, INForA, OUTForA
  assign bit_extender_1_out = {{15{1'b0}}, or_2_out};  // Bit_Extender bit_extender_1
  // Probe on M_PC[11:0]
  D_Flip_Flop #(.trigger("high"), .Pre_Clr_Positions("LEGACY"), .NegatePresetClear("false"), .enable("true"), .NewFFLayout("false")) d_ff_1 (.Q(d_ff_1_q));  // open: clk, D, Qn, preset, en, reset
  // Probe on 13'h377
  Adder #(.width(16)) adder_4 (.a(\无条件分支数 ), .b(bit_extender_1_out), .out(adder_4_out));  // open: cin, cout
  // Probe on WB_PC[11:0]
  Comparator #(.width(13), .mode("twosComplement")) comparator_1 (
    .a(CNT_num), .b(13'h377), .eq(comparator_1_eq), .lt(comparator_1_lt));  // open: gt
  Clock #(.highDuration(1), .lowDuration(1)) clock_1 (.out(clock_1_out));
  \单周期硬布线控制器  \u_单周期硬布线控制器_1  (
    .Funct({ID_IR[30], ID_IR[25], ID_IR[14:12]}), .OP(ID_IR[6:2]), .ALU_OP(\单周期硬布线控制器_1_alu_op ),
    .MemToReg(\单周期硬布线控制器_1_memtoreg ), .MemWrite(\单周期硬布线控制器_1_memwrite ), .ALU_SRC(\单周期硬布线控制器_1_alu_src ),
    .RegWrite(\单周期硬布线控制器_1_regwrite ), .ecall(\单周期硬布线控制器_1_ecall ), .S_type(SType),
    .Jalr(\单周期硬布线控制器_1_jalr ), .Beq(\单周期硬布线控制器_1_beq ), .JAL(\单周期硬布线控制器_1_jal ), .Bne(\单周期硬布线控制器_1_bne ),
    .IR(ID_IR[21]), .uret(URET), .Bge(\单周期硬布线控制器_1_bge ), .sb(\单周期硬布线控制器_1_sb ), .ALT(\单周期硬布线控制器_1_alt ),
    .RsUsed(RsUsed), .RtUsed(RtUsed));  // open: IRE, IRD
  Multiplexer #(.select(1), .width(5), .disabled("Z"), .enable("false")) multiplexer_6 (
    .in0(ID_IR[19:15]), .in1(5'b01010), .out(Rs), .sel(\单周期硬布线控制器_1_ecall ));
  Multiplexer #(.select(1), .width(5), .disabled("Z"), .enable("false")) multiplexer_7 (
    .in0(ID_IR[24:20]), .in1(5'b10001), .out(Rt), .sel(\单周期硬布线控制器_1_ecall ));
  Multiplexer #(.select(1), .width(12), .disabled("Z"), .enable("false")) multiplexer_8 (
    .in0(ID_IR[31:20]), .in1({ID_IR[31:25], ID_IR[11:7]}), .out(multiplexer_8_out), .sel(SType));
  nand nand_1 (nand_1_out, d_ff_1_q, comparator_1_eq);
  Counter #(.width(13), .max('h1fff), .ongoal("stay"), .trigger("rising"), .behavior("old")) counter_1 (
    .count(comparator_1_lt), .Q(CNT_num), .clk(clock_1_out));  // open: load, D, carry, clr, preset
  assign bit_extender_2_out = {{20{multiplexer_8_out[11]}}, multiplexer_8_out};  // Bit_Extender bit_extender_2
  assign bit_extender_3_out = {{8{ID_IR[31]}}, {ID_IR[31], ID_IR[7], ID_IR[30:25], ID_IR[11:8]}};  // Bit_Extender bit_extender_3
  Multiplexer #(.select(1), .width(20), .disabled("Z"), .enable("false")) multiplexer_9 (
    .in0(bit_extender_3_out), .in1({ID_IR[31], ID_IR[19:12], ID_IR[20], ID_IR[30:21]}),
    .out(multiplexer_9_out), .sel(\单周期硬布线控制器_1_jal ));
  assign controlled_buffer_1_out = nand_1_out ? clock_1_out : 1'bz;  // Controlled_Buffer controlled_buffer_1
  Regifile regifile_1 (
    .Din(RDin), .Clk(CLK), .R1(regifile_1_r1), .R2(regifile_1_r2), .WE(RegWrite), .W_num(WBAddr),
    .R1_num(Rs), .R2_num(Rt));
  not not_3 (not_3_out, JAL);
  not not_4 (not_4_out, JALR);
  Pull_Resistor #(.pull(1)) pull_resistor_1 (.node(controlled_buffer_1_out));
  assign bit_extender_4_out = {{12{multiplexer_9_out[19]}}, multiplexer_9_out};  // Bit_Extender bit_extender_4
  Register #(.width(16), .trigger("rising"), .Select("low")) \u_条件分支成功数  (
    .D(adder_5_out), .Q(\条件分支成功数 ), .clk(CLK), .clr(RST));  // open: en
  and and_1 (and_1_out, not_3_out, PCSrc, not_4_out);
  not not_5 (not_5_out, halt);
  Flow_Register_Bit ID_EX (
    .IN4(\单周期硬布线控制器_1_alt ), .IN3(\单周期硬布线控制器_1_jal ), .IN2(\单周期硬布线控制器_1_jalr ), .IN5(\单周期硬布线控制器_1_bge ),
    .IN6(\单周期硬布线控制器_1_sb ), .IN1(\单周期硬布线控制器_1_ecall ), .OUT4(ALT), .OUT3(JAL), .OUT2(JALR), .OUT5(Bge),
    .OUT6(ID_EX_out6), .OUT1(ecall), .Flush(Flush), .CLK(CLK), .RST(RST));  // open: IN7, OUT7, ALUOPIN, ALUOPOut, EN
  Flow_Register_Bit flow_register_bit_1 (
    .IN4(\单周期硬布线控制器_1_beq ), .IN3(\单周期硬布线控制器_1_bne ), .IN2(\单周期硬布线控制器_1_memtoreg ),
    .IN5(\单周期硬布线控制器_1_memwrite ), .IN1(\单周期硬布线控制器_1_alu_src ), .OUT4(flow_register_bit_1_out4),
    .OUT3(flow_register_bit_1_out3), .OUT2(MEMRead), .OUT5(flow_register_bit_1_out5),
    .OUT1(flow_register_bit_1_out1), .Flush(Flush), .CLK(CLK), .RST(RST), .IN7(\单周期硬布线控制器_1_regwrite ),
    .OUT7(flow_register_bit_1_out7), .ALUOPIN(\单周期硬布线控制器_1_alu_op ), .ALUOPOut(flow_register_bit_1_aluopout));  // open: IN6, OUT6, EN
  Flow_Register flow_register_1 (
    .IN1(regifile_1_r1), .Flush(Flush), .CLK(CLK), .OUT1(flow_register_1_out1), .PC(ID_IR), .PC_2(EX_IR),
    .PC2(ID_PC), .PC2_2(EX_PC), .RST(RST), .IN2(regifile_1_r2), .OUT2(flow_register_1_out2),
    .IN3(bit_extender_4_out), .OUT3(flow_register_1_out3), .IN4(bit_extender_2_out),
    .OUT4(flow_register_1_out4), .INrd(ID_IR[11:7]), .OUTrd(flow_register_1_outrd),
    .INcor(fowarding_logic_1_rsforward), .OUTcor(flow_register_1_outcor),
    .INForA(fowarding_logic_1_rtforward), .OUTForA(flow_register_1_outfora));  // open: EN
  assign bit_extender_5_out = {{15{1'b0}}, and_1_out};  // Bit_Extender bit_extender_5
  and and_2 (CLK, controlled_buffer_1_out, not_5_out);
  Multiplexer #(.select(2), .width(32), .disabled("Z"), .enable("false")) multiplexer_10 (
    .in0(flow_register_1_out1), .in1(RDin), .in2(ForEX), .out(multiplexer_10_out),
    .sel(flow_register_1_outcor));  // open: in3
  Multiplexer #(.select(2), .width(32), .disabled("Z"), .enable("false")) multiplexer_11 (
    .in0(flow_register_1_out2), .in1(RDin), .in2(ForEX), .out(multiplexer_11_out),
    .sel(flow_register_1_outfora));  // open: in3
  Adder #(.width(16)) adder_5 (.a(\条件分支成功数 ), .b(bit_extender_5_out), .out(adder_5_out));  // open: cin, cout
  Multiplexer #(.select(1), .width(32), .disabled("Z"), .enable("false")) multiplexer_12 (
    .in0(multiplexer_11_out), .in1(flow_register_1_out4), .out(multiplexer_12_out),
    .sel(flow_register_bit_1_out1));
  ALU alu_1 (
    .X(multiplexer_10_out), .Y(multiplexer_12_out), .AluOP(flow_register_bit_1_aluopout),
    .Equal(alu_1_equal), .Result(ALUO), .Result_2(alu_1_result_2), .out_4(alu_1_out_4));  // open: out_6
  Register #(.width(2), .trigger("rising"), .Select("low")) register_1 (
    .D(IREncode), .en(IRespond), .Q(register_1_q), .clk(CLK));  // open: clr
  Shifter #(.width(32), .shift("ll")) shifter_1 (.in(flow_register_1_out3), .\dist (5'b00001), .out(PCOffset));
  assign bit_extender_6_out = {{15{1'b0}}, PCSrc};  // Bit_Extender bit_extender_6
  assign bit_extender_7_out = {{15{1'b0}}, Flush};  // Bit_Extender bit_extender_7
  not not_6 (not_6_out, PCSrc);
  and and_3 (and_3_out, flow_register_bit_1_out3, not_7_out);
  not not_7 (not_7_out, alu_1_equal);
  Comparator #(.width(32), .mode("twosComplement")) comparator_2 (
    .a(multiplexer_11_out), .b(32'h22), .eq(comparator_2_eq));  // open: gt, lt
  not not_8 (not_8_out, comparator_2_eq);
  Multiplexer #(.select(2), .width(5), .disabled("Z"), .enable("false")) multiplexer_13 (
    .in0({5{1'b0}}), .in1(5'b01000), .in2(5'b10000), .in3(5'b11000), .out(multiplexer_13_out), .sel(ALUO[1:0]));
  Register #(.width(16), .trigger("rising"), .Select("low")) \u_气泡数  (
    .D(adder_7_out), .Q(\插入气泡数 ), .clk(CLK), .clr(RST));  // open: en
  Register #(.width(16), .trigger("rising"), .Select("low")) \LoadUse数  (
    .D(adder_8_out), .Q(\LoadUse次数 ), .clk(CLK), .clr(RST));  // open: en
  and and_4 (and_4_out, not_6_out, Flush);
  Demultiplexer #(.select(2), .width(1), .tristate("false"), .disabled("Z"), .enable("false")) demultiplexer_1 (
    .out1(demultiplexer_1_out1), .out2(demultiplexer_1_out2), .out3(demultiplexer_1_out3), .in(URET),
    .sel(register_1_q));  // open: out0
  and and_5 (and_5_out, alu_1_out_4, Bge);
  and and_6 (and_6_out, flow_register_bit_1_out4, alu_1_equal);
  and and_7 (and_7_out, ecall, comparator_2_eq);
  and and_8 (and_8_out, ecall, not_8_out);
  Multiplexer #(.select(1), .width(32), .disabled("Z"), .enable("false")) multiplexer_14 (
    .in0(ALUO), .in1(alu_1_result_2), .out(multiplexer_14_out), .sel(ALT));
  Shifter #(.width(32), .shift("ll")) shifter_2 (
    .in(multiplexer_11_out), .\dist (multiplexer_13_out), .out(shifter_2_out));
  Adder #(.width(16)) adder_6 (.a(bit_extender_6_out), .b(bit_extender_7_out), .out(adder_6_out));  // open: cin, cout
  assign bit_extender_8_out = {{15{1'b0}}, and_4_out};  // Bit_Extender bit_extender_8
  or or_3 (PCSrc, and_3_out, and_6_out, and_5_out, JAL, JALR);
  Register #(.width(32), .trigger("rising"), .Select("low")) LED_Register (
    .D(multiplexer_10_out), .en(and_7_out), .Q(LedData), .clk(CLK), .clr(RST));
  Adder #(.width(16)) adder_7 (.a(\插入气泡数 ), .b(adder_6_out), .out(adder_7_out));  // open: cin, cout
  Adder #(.width(16)) adder_8 (.a(\LoadUse次数 ), .b(bit_extender_8_out), .out(adder_8_out));  // open: cin, cout
  \中断按键参考电路  \u_中断按键参考电路_1  (
    .IRO(\中断按键参考电路_1_iro ), .\同步清零信号 (demultiplexer_1_out1), .IR(IR1), .IR_Light(W1), .CLK(CLK));  // open: IROI, IROI_CLR, IROR
  \中断按键参考电路  \u_中断按键参考电路_2  (
    .IRO(\中断按键参考电路_2_iro ), .\同步清零信号 (demultiplexer_1_out2), .IR(IR2), .IR_Light(W2), .CLK(CLK));  // open: IROI, IROI_CLR, IROR
  \中断按键参考电路  \u_中断按键参考电路_3  (
    .IRO(\中断按键参考电路_3_iro ), .\同步清零信号 (demultiplexer_1_out3), .IR(IR3), .IR_Light(W3), .CLK(CLK));  // open: IROI, IROI_CLR, IROR
  or or_4 (or_4_out, JALR, JAL);
  assign bit_extender_9_out = {{2{1'b0}}, ALUO[31:2]};  // Bit_Extender bit_extender_9
  Adder #(.width(32)) adder_9 (.a(32'h4), .b(EX_PC), .out(adder_9_out));  // open: cin, cout
  Multiplexer #(.select(1), .width(32), .disabled("Z"), .enable("false")) multiplexer_15 (
    .in0(multiplexer_14_out), .in1(adder_9_out), .out(multiplexer_15_out), .sel(or_4_out));
  Priority_Encoder #(.select(2), .disabled("Z")) priority_encoder_1 (
    .in1(\中断按键参考电路_1_iro ), .in2(\中断按键参考电路_2_iro ), .in3(\中断按键参考电路_3_iro ), .out(IREncode),
    .gs(priority_encoder_1_gs));  // open: in0, en_out, en_in
  Flow_Register_Bit EX_MEM (
    .IN3(flow_register_bit_1_out7), .IN2(ID_EX_out6), .IN5(MEMRead), .IN1(flow_register_bit_1_out5),
    .OUT3(EX_MEM_out3), .OUT2(sb), .OUT5(EX_MEM_out5), .OUT1(MemWrite), .Flush(1'b0), .CLK(CLK), .RST(RST),
    .IN7(and_8_out), .OUT7(EX_MEM_out7));  // open: IN4, IN6, OUT4, OUT6, ALUOPIN, ALUOPOut, EN
  Flow_Register flow_register_2 (
    .IN1(multiplexer_15_out), .Flush(1'b0), .CLK(CLK), .OUT1(ForEX), .PC(EX_IR), .PC_2(MEM_IR), .PC2(EX_PC),
    .PC2_2(M_PC), .RST(RST), .IN3(shifter_2_out), .OUT3(MDin), .IN4(bit_extender_9_out),
    .OUT4(flow_register_2_out4), .INrd(flow_register_1_outrd), .OUTrd(flow_register_2_outrd),
    .INcor(ALUO[1:0]), .OUTcor(flow_register_2_outcor));  // open: IN2, OUT2, EN, INForA, OUTForA
  and and_9 (IRespond, priority_encoder_1_gs, IE);
  Bit_Extender #(.in_width(32), .out_width(20), .\type ("zero")) bit_extender_10 (
    .in(flow_register_2_out4), .out(bit_extender_10_out));
  Shifter #(.width(4), .shift("ll")) shifter_3 (.in(4'b0001), .\dist (flow_register_2_outcor), .out(shifter_3_out));
  not not_9 (not_9_out, IRespond);
  Comparator #(.width(16), .mode("twosComplement")) comparator_3 (
    .a(\总周期数 ), .b({16{1'b0}}), .eq(comparator_3_eq));  // open: gt, lt
  // MIPS_RAM mips_ram_1: pin names not known; wires that end beside it: bit_extender_10_out, MDin, MemWrite, MemSel, CLK, RST, mips_ram_1_p7, MEM_IR
  Multiplexer #(.select(1), .width(4), .disabled("Z"), .enable("false")) multiplexer_16 (
    .in0(4'b1111), .in1(shifter_3_out), .out(MemSel), .sel(sb));
  or or_5 (or_5_out, IRespond, URET);
  Register #(.width(1), .trigger("rising"), .Select("low")) u_IE (
    .D(not_9_out), .en(or_5_out), .Q(IE), .clk(CLK), .preset(comparator_3_eq));  // open: clr, cs
  Flow_Register_Bit MEM_WB (
    .IN3(EX_MEM_out3), .IN5(EX_MEM_out5), .OUT3(RegWrite), .OUT5(MTR), .Flush(1'b0), .CLK(CLK), .RST(RST),
    .IN7(EX_MEM_out7), .OUT7(go_halt));  // open: IN4, IN2, IN6, IN1, OUT4, OUT2, OUT6, OUT1, ALUOPIN, ALUOPOut, EN
  Flow_Register flow_register_3 (
    .IN1(ForEX), .Flush(1'b0), .CLK(CLK), .OUT1(flow_register_3_out1), .PC(MEM_IR), .PC_2(WB_IR), .PC2(M_PC),
    .PC2_2(WB_PC), .RST(RST), .IN3(mips_ram_1_p7), .OUT3(flow_register_3_out3), .INrd(flow_register_2_outrd),
    .OUTrd(WBAddr));  // open: IN2, OUT2, IN4, OUT4, INcor, OUTcor, EN, INForA, OUTForA
  Multiplexer #(.select(1), .width(32), .disabled("Z"), .enable("false")) multiplexer_17 (
    .in0(flow_register_3_out1), .in1(flow_register_3_out3), .out(RDin), .sel(MTR));

  // Other names for the same wires on the sheet: ForMEM[31:0] = RDin; MEM_PC[31:0] = M_PC; PCSig[31:0] = EX_PC

  // Notes on the sheet:
  //   中断源
  //   时空图监测，可删除
  //   中断等待指示
  //   数码管输出
  //   指令存储器
  //   contents of rom_1 (hex, n*v repeats v):
  //   100493 100006f 100493 200913 300993 100006f 100493 200913 300993 100006f 100493 200913 300993
  //   100006f 100493 200913 300993 394000ef 100413 100493 1f49493 900533 2200893 73 24d493 48463 fedff06f
  //   900533 2200893 73 100493 249493 900533 2200893 73 48463 fedff06f 100493 1f49493 900533 2200893 73
  //   4034d493 900533 2200893 73 4044d493 900533 2200893 73 4044d493 900533 2200893 73 4044d493 900533
  //   2200893 73 4044d493 900533 2200893 73 4044d493 900533 2200893 73 4044d493 900533 2200893 73 4044d493
  //   900533 2200893 73 100413 1f41993 41f9d993 433 c00913 300b13 140413 f47413 800293 100313 499993
  //   89e9b3 1300533 2200893 73 406282b3 fe0294e3 140413 f00f93 1f47433 1c41413 800293 100313 49d993
  //   89e9b3 1300533 2200893 73 406282b3 fe0294e3 1c45413 406b0b33 b0463 f95ff06f 2b3 fff2c293 829293
  //   ff2e293 500533 2200893 73 fff00413 493 84a023 140413 448493 84a023 140413 448493 84a023 140413
  //   448493 84a023 140413 448493 84a023 140413 448493 84a023 140413 448493 84a023 140413 448493 84a023
  //   140413 448493 84a023 140413 448493 84a023 140413 448493 84a023 140413 448493 84a023 140413 448493
  //   84a023 140413 448493 84a023 140413 448493 84a023 140413 448493 84a023 140413 448493 140413 433
  //   3c00493 42983 4aa03 149a2b3 28663 134a023 1442023 ffc48493 fe9412e3 800533 2200893 73 440413 3c00493
  //   fc9416e3 200293 1100493 849493 1148493 1049493 900533 2200893 73 1c00e13 254d4b3 900533 2200893 73
  //   fffe0e13 fe0e16e3 a00893 73 8800493 849493 4848493 8700913 891913 5490913 2997933 1091913 11096913
  //   1200533 2200893 73 a00893 73 313 2000e13 493 100913 930023 900533 2200893 73 12484b3 130313 fffe0e13
  //   fe0e12e3 800e13 313 32483 900533 2200893 73 430313 fffe0e13 fe0e14e3 a00893 73 f00493 900533 2200893
  //   73 fff48493 fe04d8e3 a00893 73 a00893 73 413 140413 800533 2200893 73 240413 800533 2200893 73
  //   340413 800533 2200893 73 440413 800533 2200893 73 540413 800533 2200893 73 640413 800533 2200893 73
  //   740413 800533 2200893 73 840413 800533 2200893 2200893 73 8067
  //   控制位
  //   指令字
  //   流水调试日志用
  //   暂停节拍，不能为0
  //   JAL
  //   JALR
  //   URET
  //   Bge
  //   BEQ offset
  //   JAL offset
  //   戳工具置1进入计数暂停模式，ctrl+k时钟自动运行到对应节拍暂停
  //   ctrl+k关闭时钟连续运行，将控制位置零，进入单步调试模式调试
  //   用这个时钟源需要去掉电路中的其他时钟源
  //   Beq
  //   Bne
  //   MemToReg
  //   MemWrite
  //   AluOP
  //   AluSrcB
  //   RegWrite
  //   S_Type
  //   ecall
  //   可计数暂停的时钟源
  //   rd
  //   为方便自动评测，需要输出流水线各段保存的PC值，注意是PC不是PC+4，另外ID段寄存器写入信息，Mem段内存写入信息也要输出
  //   Beq Judge
  //   Bne Judge
  //   Bge Judge
  //   rd
  //   rd
endmodule

module \中断按键参考电路  (
  input  IROI_CLR,
  input  CLK,
  input  IR,
  input  \同步清零信号 ,
  output IROI,
  output IRO,
  output IROR,
  output IR_Light
);

  wire and_1_out, and_2_out, d_ff_1_q, IRRunning_qn, or_2_out, or_3_out, or_4_out;

  or or_1 (IR_Light, IRO, d_ff_1_q);
  D_Flip_Flop #(.trigger("rising"), .Pre_Clr_Positions("LEGACY"), .NegatePresetClear("false"), .enable("true"), .NewFFLayout("false")) d_ff_1 (
    .clk(IR), .D(1'b1), .Q(d_ff_1_q), .reset(IRO));  // open: Qn, preset, en
  or or_2 (or_2_out, d_ff_1_q, IRO);
  and and_1 (and_1_out, or_2_out, ~\同步清零信号 );  // AND_Gate
  D_Flip_Flop #(.trigger("rising"), .Pre_Clr_Positions("LEGACY"), .NegatePresetClear("false"), .enable("true"), .NewFFLayout("false")) IR1 (
    .clk(CLK), .D(and_1_out), .Q(IRO));  // open: Qn, preset, en, reset
  and and_2 (and_2_out, and_1_out, IRRunning_qn);
  or or_3 (or_3_out, IROI_CLR, IROR);
  D_Flip_Flop #(.trigger("falling"), .Pre_Clr_Positions("LEGACY"), .NegatePresetClear("false"), .enable("true"), .NewFFLayout("false")) IR2 (
    .clk(CLK), .D(and_2_out), .Q(IROI), .en(or_3_out));  // open: Qn, preset, reset
  D_Flip_Flop #(.trigger("rising"), .Pre_Clr_Positions("LEGACY"), .NegatePresetClear("false"), .enable("true"), .NewFFLayout("false")) IRRunning (
    .clk(CLK), .D(and_1_out), .Q(IROR), .Qn(IRRunning_qn), .en(or_4_out));  // open: preset, reset
  or or_4 (or_4_out, IROI_CLR, \同步清零信号 );

  // Notes on the sheet:
  //   中断信号采样参考电路
  //   Reset 
endmodule

module \单周期_单级中断  (
  input  IR1,
  input  IR2,
  input  IR3,
  output RegWrite,
  output MemWrite,
  output [31:0] PC,
  output [31:0] IR,
  output [31:0] RDin,
  output [31:0] MDin,
  output [31:0] LedData
);

  wire ALT, alu_1_equal, alu_1_out_4, and_1_out, and_3_out, and_4_out, and_5_out, and_6_out, Bge, CLK,
       clock_1_out, comparator_1_eq, comparator_2_eq, comparator_3_eq, comparator_4_eq, comparator_5_eq,
       comparator_5_lt, comparator_6_eq, comparator_7_eq, d_ff_1_q, demultiplexer_1_out1,
       demultiplexer_1_out2, demultiplexer_1_out3, ecall, Go, go_halt, halt, IE, IR1_t, IR2_t, IR3_t, IRA,
       IRB, IRC, IRespond, JAL, JALR, MTR, nand_1_out, not_1_out, not_2_out, not_3_out, not_4_out, not_5_out,
       not_6_out, or_1_out, or_3_out, or_5_out, or_7_out, or_9_out, PCSrc, priority_encoder_1_gs, RST, sb,
       SType, URET, W1, W2, W3, \中断按键参考电路_1_iro , \中断按键参考电路_2_iro , \中断按键参考电路_3_iro , \单周期硬布线控制器_1_alu_src ,
       \单周期硬布线控制器_1_beq , \单周期硬布线控制器_1_bne ;
  wire [1:0] IREncode, register_1_q;
  wire [3:0] MemSel, shifter_3_out, \单周期硬布线控制器_1_alu_op ;
  wire [4:0] multiplexer_6_out, multiplexer_7_out, multiplexer_12_out;
  wire [11:0] multiplexer_8_out;
  wire [12:0] CNT_num;
  wire [15:0] adder_1_out, \总周期数 ;
  wire [19:0] bit_extender_1_out, bit_extender_4_out, multiplexer_9_out, shifter_1_out;
  wire [31:0] adder_2_out, adder_3_out, alu_1_result, alu_1_result_2, ALUO, bit_extender_2_out, IAddr,
       mEPC_q, mips_ram_1_p7, multiplexer_1_out, multiplexer_2_out, multiplexer_3_out, multiplexer_4_out,
       multiplexer_10_out, multiplexer_15_out, PCOffset, regifile_1_r1, regifile_1_r2;

  Button \u_继续运行  (.out(Go));
  Button _1 ();  // open: out
  Button _2 ();  // open: out
  Button _3 ();  // open: out
  LED #(.active("true")) led_1 (.in(W1));
  LED #(.active("true")) led_2 (.in(W2));
  LED #(.active("true")) led_3 (.in(W3));
  Hex_Digit_Display hex_digit_display_1 (.value(LedData[31:28]));  // open: dp
  Comparator #(.width(16), .mode("twosComplement")) comparator_1 (
    .a(16'h23b), .b(\总周期数 ), .eq(comparator_1_eq));  // open: gt, lt
  Comparator #(.width(16), .mode("twosComplement")) comparator_2 (
    .a(\总周期数 ), .b(16'h1), .eq(comparator_2_eq));  // open: gt, lt
  Comparator #(.width(16), .mode("twosComplement")) comparator_3 (
    .a(\总周期数 ), .b(16'h4), .eq(comparator_3_eq));  // open: gt, lt
  Comparator #(.width(16), .mode("twosComplement")) comparator_4 (
    .a(\总周期数 ), .b(16'h7), .eq(comparator_4_eq));  // open: gt, lt
  Hex_Digit_Display hex_digit_display_2 (.value(LedData[23:20]));  // open: dp
  Hex_Digit_Display hex_digit_display_3 (.value(LedData[27:24]));  // open: dp
  or or_1 (or_1_out, comparator_1_eq, comparator_2_eq);
  assign IRA = or_1_out ? ~CLK : 1'bz;  // Controlled_Inverter controlled_inverter_1
  assign IRB = comparator_3_eq ? ~CLK : 1'bz;  // Controlled_Inverter controlled_inverter_2
  assign IRC = comparator_4_eq ? ~CLK : 1'bz;  // Controlled_Inverter controlled_inverter_3
  Hex_Digit_Display hex_digit_display_4 (.value(LedData[15:12]));  // open: dp
  Hex_Digit_Display hex_digit_display_5 (.value(LedData[19:16]));  // open: dp
  Pull_Resistor #(.pull(0)) pull_resistor_1 (.node(IRA));
  Pull_Resistor #(.pull(0)) pull_resistor_2 (.node(IRB));
  Pull_Resistor #(.pull(0)) pull_resistor_3 (.node(IRC));
  Hex_Digit_Display hex_digit_display_6 (.value(LedData[11:8]));  // open: dp
  Hex_Digit_Display hex_digit_display_7 (.value(LedData[7:4]));  // open: dp
  // Probe on \总周期数 
  Hex_Digit_Display hex_digit_display_8 (.value(LedData[3:0]));  // open: dp
  not not_1 (not_1_out, halt);
  or or_2 (IR1_t, IR1, IRA);
  Register #(.width(16), .trigger("rising"), .Select("low")) \u_周期  (
    .D(adder_1_out), .en(not_1_out), .Q(\总周期数 ), .clk(CLK), .clr(RST));
  or or_3 (or_3_out, Go, and_1_out);
  not not_2 (not_2_out, go_halt);
  or or_4 (IR2_t, IR2, IRB);
  and and_1 (and_1_out, not_2_out, not_3_out);
  not not_3 (not_3_out, halt);
  Multiplexer #(.select(1), .width(32), .disabled("Z"), .enable("false")) multiplexer_1 (
    .in0(multiplexer_3_out), .in1(IAddr), .out(multiplexer_1_out), .sel(or_5_out));
  or or_5 (or_5_out, URET, IRespond);
  Adder #(.width(16)) adder_1 (.a(\总周期数 ), .b(16'h1), .out(adder_1_out));  // open: cin, cout
  Register #(.width(32), .trigger("rising"), .Select("low")) u_PC (
    .D(multiplexer_1_out), .en(or_3_out), .Q(PC), .clk(CLK), .clr(RST));
  or or_6 (IR3_t, IR3, IRC);
  Adder #(.width(32)) adder_2 (.a(PC), .b(PCOffset), .out(adder_2_out));  // open: cin, cout
  Register #(.width(1), .trigger("rising"), .Select("low")) u_Halt (.D(go_halt), .Q(halt), .clk(CLK));  // open: en, clr
  Adder #(.width(32)) adder_3 (.a(PC), .b(32'h4), .out(adder_3_out));  // open: cin, cout
  Multiplexer #(.select(1), .width(32), .disabled("Z"), .enable("false")) multiplexer_2 (
    .in0(adder_2_out), .in1(ALUO), .out(multiplexer_2_out), .sel(JALR));
  Multiplexer #(.select(1), .width(32), .disabled("Z"), .enable("false")) multiplexer_3 (
    .in0(adder_3_out), .in1(multiplexer_2_out), .out(multiplexer_3_out), .sel(PCSrc));
  ROM #(.addrWidth(10), .dataWidth(32), .Select("high")) rom_1 (.addr(PC[11:2]), .data(IR));
  Register #(.width(32), .trigger("rising"), .Select("low")) mEPC (
    .D(multiplexer_3_out), .en(IRespond), .Q(mEPC_q), .clk(CLK));  // open: clr
  // RiscV_Probe riscv_probe_1: pin names not known; wires that end beside it: IR
  Multiplexer #(.select(2), .width(32), .disabled("Z"), .enable("false")) multiplexer_4 (
    .in1(32'h30ac), .in2(32'h3150), .in3(32'h31f4), .out(multiplexer_4_out), .sel(IREncode));  // open: in0
  Multiplexer #(.select(1), .width(32), .disabled("Z"), .enable("false")) multiplexer_5 (
    .in0(multiplexer_4_out), .in1(mEPC_q), .out(IAddr), .sel(URET));
  Register #(.width(2), .trigger("rising"), .Select("low")) register_1 (
    .D(IREncode), .en(IRespond), .Q(register_1_q), .clk(CLK));  // open: clr
  \单周期硬布线控制器  \u_单周期硬布线控制器_1  (
    .Funct({IR[30], IR[25], IR[14:12]}), .OP(IR[6:2]), .ALU_OP(\单周期硬布线控制器_1_alu_op ), .MemToReg(MTR),
    .MemWrite(MemWrite), .ALU_SRC(\单周期硬布线控制器_1_alu_src ), .RegWrite(RegWrite), .ecall(ecall), .S_type(SType),
    .Jalr(JALR), .Beq(\单周期硬布线控制器_1_beq ), .JAL(JAL), .Bne(\单周期硬布线控制器_1_bne ), .IR(IR[21]), .uret(URET),
    .Bge(Bge), .sb(sb), .ALT(ALT));  // open: RsUsed, RtUsed, IRE, IRD
  Multiplexer #(.select(1), .width(5), .disabled("Z"), .enable("false")) multiplexer_6 (
    .in0(IR[19:15]), .in1(5'b01010), .out(multiplexer_6_out), .sel(ecall));
  Multiplexer #(.select(1), .width(5), .disabled("Z"), .enable("false")) multiplexer_7 (
    .in0(IR[24:20]), .in1(5'b10001), .out(multiplexer_7_out), .sel(ecall));
  Multiplexer #(.select(1), .width(12), .disabled("Z"), .enable("false")) multiplexer_8 (
    .in0(IR[31:20]), .in1({IR[31:25], IR[11:7]}), .out(multiplexer_8_out), .sel(SType));
  assign bit_extender_1_out = {{8{IR[31]}}, {IR[31], IR[7], IR[30:25], IR[11:8]}};  // Bit_Extender bit_extender_1
  D_Flip_Flop #(.trigger("high"), .Pre_Clr_Positions("LEGACY"), .NegatePresetClear("false"), .enable("true"), .NewFFLayout("false")) d_ff_1 (.Q(d_ff_1_q));  // open: clk, D, Qn, preset, en, reset
  // Probe on 13'hbb
  Demultiplexer #(.select(2), .width(1), .tristate("false"), .disabled("Z"), .enable("false")) demultiplexer_1 (
    .out1(demultiplexer_1_out1), .out2(demultiplexer_1_out2), .out3(demultiplexer_1_out3), .in(URET),
    .sel(register_1_q));  // open: out0
  assign bit_extender_2_out = {{20{multiplexer_8_out[11]}}, multiplexer_8_out};  // Bit_Extender bit_extender_2
  Multiplexer #(.select(1), .width(20), .disabled("Z"), .enable("false")) multiplexer_9 (
    .in0(bit_extender_1_out), .in1({IR[31], IR[19:12], IR[20], IR[30:21]}), .out(multiplexer_9_out), .sel(JAL));
  Comparator #(.width(13), .mode("twosComplement")) comparator_5 (
    .a(CNT_num), .b(13'hbb), .eq(comparator_5_eq), .lt(comparator_5_lt));  // open: gt
  Clock #(.highDuration(1), .lowDuration(1)) clock_1 (.out(clock_1_out));
  Regifile regifile_1 (
    .Din(RDin), .Clk(CLK), .R1(regifile_1_r1), .R2(regifile_1_r2), .WE(RegWrite), .W_num(IR[11:7]),
    .R1_num(multiplexer_6_out), .R2_num(multiplexer_7_out));
  or or_7 (or_7_out, JALR, JAL);
  Counter #(.width(13), .max('h1fff), .ongoal("stay"), .trigger("rising"), .behavior("old")) counter_1 (
    .count(comparator_5_lt), .Q(CNT_num), .clk(clock_1_out));  // open: load, D, carry, clr, preset
  \中断按键参考电路  \u_中断按键参考电路_1  (
    .IRO(\中断按键参考电路_1_iro ), .\同步清零信号 (demultiplexer_1_out1), .IR(IR1_t), .IR_Light(W1), .CLK(CLK));  // open: IROI, IROI_CLR, IROR
  \中断按键参考电路  \u_中断按键参考电路_2  (
    .IRO(\中断按键参考电路_2_iro ), .\同步清零信号 (demultiplexer_1_out2), .IR(IR2_t), .IR_Light(W2), .CLK(CLK));  // open: IROI, IROI_CLR, IROR
  \中断按键参考电路  \u_中断按键参考电路_3  (
    .IRO(\中断按键参考电路_3_iro ), .\同步清零信号 (demultiplexer_1_out3), .IR(IR3_t), .IR_Light(W3), .CLK(CLK));  // open: IROI, IROI_CLR, IROR
  Multiplexer #(.select(1), .width(32), .disabled("Z"), .enable("false")) multiplexer_10 (
    .in0(regifile_1_r2), .in1(bit_extender_2_out), .out(multiplexer_10_out), .sel(\单周期硬布线控制器_1_alu_src ));
  Multiplexer #(.select(1), .width(32), .disabled("Z"), .enable("false")) multiplexer_11 (
    .in0(multiplexer_15_out), .in1(adder_3_out), .out(RDin), .sel(or_7_out));
  nand nand_1 (nand_1_out, d_ff_1_q, comparator_5_eq);
  ALU alu_1 (
    .X(regifile_1_r1), .Y(multiplexer_10_out), .AluOP(\单周期硬布线控制器_1_alu_op ), .Equal(alu_1_equal),
    .Result(alu_1_result), .Result_2(alu_1_result_2), .out_4(alu_1_out_4));  // open: out_6
  Shifter #(.width(20), .shift("ll")) shifter_1 (.in(multiplexer_9_out), .\dist (5'b00001), .out(shifter_1_out));
  assign CLK = nand_1_out ? clock_1_out : 1'bz;  // Controlled_Buffer controlled_buffer_1
  Pull_Resistor #(.pull(1)) pull_resistor_4 (.node(CLK));
  Priority_Encoder #(.select(2), .disabled("Z")) priority_encoder_1 (
    .in1(\中断按键参考电路_1_iro ), .in2(\中断按键参考电路_2_iro ), .in3(\中断按键参考电路_3_iro ), .out(IREncode),
    .gs(priority_encoder_1_gs));  // open: in0, en_out, en_in
  not not_4 (not_4_out, alu_1_equal);
  Multiplexer #(.select(2), .width(5), .disabled("Z"), .enable("false")) multiplexer_12 (
    .in0({5{1'b0}}), .in1(5'b01000), .in2(5'b10000), .in3(5'b11000), .out(multiplexer_12_out),
    .sel(alu_1_result[1:0]));
  assign PCOffset = {{12{shifter_1_out[19]}}, shifter_1_out};  // Bit_Extender bit_extender_3
  and and_2 (IRespond, priority_encoder_1_gs, IE);
  and and_3 (and_3_out, alu_1_out_4, Bge);
  and and_4 (and_4_out, \单周期硬布线控制器_1_bne , not_4_out);
  and and_5 (and_5_out, ecall, comparator_6_eq);
  Comparator #(.width(32), .mode("twosComplement")) comparator_6 (
    .a(regifile_1_r2), .b(32'h22), .eq(comparator_6_eq));  // open: gt, lt
  not not_5 (not_5_out, comparator_6_eq);
  Shifter #(.width(32), .shift("ll")) shifter_2 (.in(regifile_1_r2), .\dist (multiplexer_12_out), .out(MDin));
  and and_6 (and_6_out, \单周期硬布线控制器_1_beq , alu_1_equal);
  Register #(.width(32), .trigger("rising"), .Select("low")) LED_Register (
    .D(regifile_1_r1), .en(and_5_out), .Q(LedData), .clk(CLK), .clr(RST));
  and and_7 (go_halt, ecall, not_5_out);
  Multiplexer #(.select(1), .width(32), .disabled("Z"), .enable("false")) multiplexer_13 (
    .in0(alu_1_result), .in1(alu_1_result_2), .out(ALUO), .sel(ALT));
  or or_8 (PCSrc, and_4_out, and_6_out, and_3_out, JAL, JALR);
  not not_6 (not_6_out, IRespond);
  or or_9 (or_9_out, IRespond, URET);
  Comparator #(.width(16), .mode("twosComplement")) comparator_7 (
    .a(\总周期数 ), .b({16{1'b0}}), .eq(comparator_7_eq));  // open: gt, lt
  Shifter #(.width(4), .shift("ll")) shifter_3 (.in(4'b0001), .\dist (alu_1_result[1:0]), .out(shifter_3_out));
  Register #(.width(1), .trigger("rising"), .Select("low")) u_IE (
    .D(not_6_out), .en(or_9_out), .Q(IE), .clk(CLK), .preset(comparator_7_eq));  // open: clr, cs
  Multiplexer #(.select(1), .width(4), .disabled("Z"), .enable("false")) multiplexer_14 (
    .in0(4'b1111), .in1(shifter_3_out), .out(MemSel), .sel(sb));
  Bit_Extender #(.in_width(30), .out_width(20), .\type ("zero")) bit_extender_4 (
    .in(alu_1_result[31:2]), .out(bit_extender_4_out));
  // MIPS_RAM mips_ram_1: pin names not known; wires that end beside it: bit_extender_4_out, MDin, MemWrite, MemSel, CLK, RST, mips_ram_1_p7
  Multiplexer #(.select(1), .width(32), .disabled("Z"), .enable("false")) multiplexer_15 (
    .in0(ALUO), .in1(mips_ram_1_p7), .out(multiplexer_15_out), .sel(MTR));

  // Notes on the sheet:
  //   中断源
  //   中断等待指示
  //   总复位信号应将除ROM以外所有存储组件全部清零
  //   单级中断测试信号模拟器
  //   数码管输出
  //   数码管输出应该用寄存器锁存，否则显示数据只能一闪而过
  //   指令存储器
  //   contents of rom_1 (hex, n*v repeats v):
  //   7d000113 100413 1f41993 41f9d993 433 c00913 800b13 140413 f47413 800293 100313 499993 89e9b3 1300533
  //   2200893 73 406282b3 fe0294e3 140413 f00f93 1f47433 1c41413 800293 100313 49d993 89e9b3 1300533
  //   2200893 73 406282b3 fe0294e3 1c45413 406b0b33 b0463 f95ff06f 2b3 fff2c293 1029293 fff2e293 500533
  //   2200893 73 f5dff06f 1112023 410113 a12023 410113 812023 410113 1312023 410113 1412023 410113 1512023
  //   410113 1612023 410113 100b13 300a13 100a93 1600433 441413 14469b3 1300533 2200893 73 fe0416e3
  //   415a0a33 fe0a10e3 ffc10113 12b03 ffc10113 12a83 ffc10113 12a03 ffc10113 12983 ffc10113 12403
  //   ffc10113 12503 ffc10113 12883 200073 1112023 410113 a12023 410113 812023 410113 1312023 410113
  //   1412023 410113 1512023 410113 1612023 410113 200b13 300a13 100a93 1600433 441413 14469b3 1300533
  //   2200893 73 fe0416e3 415a0a33 fe0a10e3 ffc10113 12b03 ffc10113 12a83 ffc10113 12a03 ffc10113 12983
  //   ffc10113 12403 ffc10113 12503 ffc10113 12883 200073 1112023 410113 a12023 410113 812023 410113
  //   1312023 410113 1412023 410113 1512023 410113 1612023 410113 300b13 300a13 100a93 1600433 441413
  //   14469b3 1300533 2200893 73 fe0416e3 415a0a33 fe0a10e3 ffc10113 12b03 ffc10113 12a83 ffc10113 12a03
  //   ffc10113 12983 ffc10113 12403 ffc10113 12503 ffc10113 12883 200073
  //   为方便自动评测，需要输出PC，IR，寄存器堆写如数据RDin
  //   指令探针
  //   RAM写使能MemWrite、RAM写入数据MDin等信号
  //   指令字
  //   JAL
  //   JALR
  //   URET
  //   Bge
  //   BEQ offset
  //   JAL offset
  //   Beq
  //   Bne
  //   MemToReg
  //   MemWrite
  //   AluOP
  //   AluSrcB
  //   RegWrite
  //   S_Type
  //   ecall
  //   rd
  //   控制位
  //   暂停节拍，不能为0
  //   可计数暂停的时钟源
  //   Bne Judge
  //   Beq Judge
  //   Bge Judge
endmodule

module \单周期_多级中断  (
  input  IR1,
  input  IR2,
  input  IR3,
  output RegWrite,
  output MemWrite,
  output [31:0] PC,
  output [31:0] IR,
  output [31:0] RDin,
  output [31:0] MDin,
  output [31:0] LedData
);

  wire ALT, alu_1_equal, alu_1_out_4, and_1_out, and_2_out, and_3_out, and_4_out, and_5_out, and_8_out, Bge,
       CLK, clock_1_out, comparator_1_eq, comparator_2_eq, comparator_3_eq, comparator_4_eq, comparator_5_eq,
       comparator_6_eq, comparator_6_lt, comparator_7_eq, comparator_8_eq, d_ff_1_q, demultiplexer_1_out1,
       demultiplexer_1_out2, demultiplexer_1_out3, demultiplexer_2_out1, demultiplexer_2_out2,
       demultiplexer_2_out3, ecall, Go, go_halt, halt, IE, IR1_t, IR2_t, IR3_t, IRA, IRB, IRC, IRD, IRE,
       IRespond, JAL, JALR, MTR, nand_1_out, not_1_out, not_2_out, not_3_out, not_4_out, not_5_out,
       not_6_out, or_1_out, or_2_out, or_4_out, or_6_out, or_8_out, or_9_out, or_10_out, or_11_out,
       or_13_out, or_14_out, PCSrc, RST, sb, SType, URET, W1, W2, W3, \中断按键参考电路_1_iro , \中断按键参考电路_1_iroi ,
       \中断按键参考电路_1_iror , \中断按键参考电路_2_iro , \中断按键参考电路_2_iroi , \中断按键参考电路_2_iror , \中断按键参考电路_3_iro ,
       \中断按键参考电路_3_iroi , \中断按键参考电路_3_iror , \单周期硬布线控制器_1_alu_src , \单周期硬布线控制器_1_beq , \单周期硬布线控制器_1_bne ;
  wire [1:0] adder_4_out, IREncode, multiplexer_5_out, multiplexer_6_out, priority_encoder_1_out,
       Stack_Pointer_q;
  wire [3:0] MemSel, shifter_3_out, \单周期硬布线控制器_1_alu_op ;
  wire [4:0] multiplexer_8_out, multiplexer_9_out, multiplexer_15_out;
  wire [11:0] multiplexer_10_out;
  wire [12:0] CNT_num;
  wire [15:0] adder_1_out, \总周期数 ;
  wire [19:0] bit_extender_1_out, bit_extender_4_out, multiplexer_12_out, shifter_1_out;
  wire [31:0] adder_2_out, adder_3_out, alu_1_result, alu_1_result_2, ALUO, bit_extender_2_out, IAddr,
       mEPC_q, mEPC_Ret, mips_ram_1_p7, multiplexer_1_out, multiplexer_2_out, multiplexer_3_out,
       multiplexer_4_out, multiplexer_7_out, multiplexer_13_out, multiplexer_18_out, PCOffset, regifile_1_r1,
       regifile_1_r2;

  Button \u_继续运行  (.out(Go));
  Button _1 ();  // open: out
  Button _2 ();  // open: out
  Button _3 ();  // open: out
  LED #(.active("true")) led_1 (.in(W1));
  LED #(.active("true")) led_2 (.in(W2));
  LED #(.active("true")) led_3 (.in(W3));
  Hex_Digit_Display hex_digit_display_1 (.value(LedData[31:28]));  // open: dp
  Comparator #(.width(16), .mode("twosComplement")) comparator_1 (
    .a(\总周期数 ), .b(16'h7), .eq(comparator_1_eq));  // open: gt, lt
  Comparator #(.width(16), .mode("twosComplement")) comparator_2 (
    .a(\总周期数 ), .b(16'h241), .eq(comparator_2_eq));  // open: gt, lt
  Hex_Digit_Display hex_digit_display_2 (.value(LedData[27:24]));  // open: dp
  Hex_Digit_Display hex_digit_display_3 (.value(LedData[23:20]));  // open: dp
  Comparator #(.width(16), .mode("twosComplement")) comparator_3 (
    .a(16'h258), .b(\总周期数 ), .eq(comparator_3_eq));  // open: gt, lt
  or or_1 (or_1_out, comparator_3_eq, comparator_4_eq);
  Comparator #(.width(16), .mode("twosComplement")) comparator_4 (
    .a(\总周期数 ), .b(16'h1), .eq(comparator_4_eq));  // open: gt, lt
  Comparator #(.width(16), .mode("twosComplement")) comparator_5 (
    .a(\总周期数 ), .b(16'h4), .eq(comparator_5_eq));  // open: gt, lt
  or or_2 (or_2_out, comparator_1_eq, comparator_2_eq);
  Hex_Digit_Display hex_digit_display_4 (.value(LedData[15:12]));  // open: dp
  Hex_Digit_Display hex_digit_display_5 (.value(LedData[19:16]));  // open: dp
  Pull_Resistor #(.pull(0)) pull_resistor_1 (.node(IRA));
  assign IRA = or_1_out ? ~CLK : 1'bz;  // Controlled_Inverter controlled_inverter_1
  Pull_Resistor #(.pull(0)) pull_resistor_2 (.node(IRB));
  assign IRB = comparator_5_eq ? ~CLK : 1'bz;  // Controlled_Inverter controlled_inverter_2
  Pull_Resistor #(.pull(0)) pull_resistor_3 (.node(IRC));
  assign IRC = or_2_out ? ~CLK : 1'bz;  // Controlled_Inverter controlled_inverter_3
  Hex_Digit_Display hex_digit_display_6 (.value(LedData[7:4]));  // open: dp
  Hex_Digit_Display hex_digit_display_7 (.value(LedData[11:8]));  // open: dp
  // Probe on \总周期数 
  Hex_Digit_Display hex_digit_display_8 (.value(LedData[3:0]));  // open: dp
  not not_1 (not_1_out, halt);
  or or_3 (IR1_t, IR1, IRA);
  Register #(.width(16), .trigger("rising"), .Select("low")) \u_周期  (
    .D(adder_1_out), .en(not_1_out), .Q(\总周期数 ), .clk(CLK), .clr(RST));
  or or_4 (or_4_out, Go, and_1_out);
  not not_2 (not_2_out, go_halt);
  or or_5 (IR2_t, IR2, IRB);
  and and_1 (and_1_out, not_2_out, not_3_out);
  not not_3 (not_3_out, halt);
  Multiplexer #(.select(1), .width(32), .disabled("Z"), .enable("false")) multiplexer_1 (
    .in0(multiplexer_3_out), .in1(IAddr), .out(multiplexer_1_out), .sel(or_6_out));
  or or_6 (or_6_out, URET, IRespond);
  Adder #(.width(16)) adder_1 (.a(\总周期数 ), .b(16'h1), .out(adder_1_out));  // open: cin, cout
  Register #(.width(32), .trigger("rising"), .Select("low")) u_PC (
    .D(multiplexer_1_out), .en(or_4_out), .Q(PC), .clk(CLK), .clr(RST));
  or or_7 (IR3_t, IR3, IRC);
  Adder #(.width(32)) adder_2 (.a(PC), .b(PCOffset), .out(adder_2_out));  // open: cin, cout
  Register #(.width(1), .trigger("rising"), .Select("low")) u_Halt (.D(go_halt), .Q(halt), .clk(CLK));  // open: en, clr
  Adder #(.width(32)) adder_3 (.a(PC), .b(32'h4), .out(adder_3_out));  // open: cin, cout
  Multiplexer #(.select(1), .width(32), .disabled("Z"), .enable("false")) multiplexer_2 (
    .in0(adder_2_out), .in1(ALUO), .out(multiplexer_2_out), .sel(JALR));
  Multiplexer #(.select(1), .width(32), .disabled("Z"), .enable("false")) multiplexer_3 (
    .in0(adder_3_out), .in1(multiplexer_2_out), .out(multiplexer_3_out), .sel(PCSrc));
  or or_8 (or_8_out, IRespond, URET);
  ROM #(.addrWidth(10), .dataWidth(32), .Select("high")) rom_1 (.addr(PC[11:2]), .data(IR));
  Register #(.width(2), .trigger("rising"), .Select("low")) Stack_Pointer (
    .D(adder_4_out), .en(or_8_out), .Q(Stack_Pointer_q), .clk(CLK));  // open: clr
  // RiscV_Probe riscv_probe_1: pin names not known; wires that end beside it: IR
  Multiplexer #(.select(1), .width(32), .disabled("Z"), .enable("false")) multiplexer_4 (
    .in0(multiplexer_3_out), .in1(mEPC_Ret), .out(multiplexer_4_out), .sel(URET));
  or or_9 (or_9_out, IRespond, URET);
  Multiplexer #(.select(1), .width(2), .disabled("Z"), .enable("false")) multiplexer_5 (
    .in0(2'b01), .in1(2'b11), .out(multiplexer_5_out), .sel(URET));
  Register #(.width(32), .trigger("rising"), .Select("low")) mEPC (
    .D(multiplexer_4_out), .en(or_9_out), .Q(mEPC_q), .clk(CLK));  // open: clr
  Multiplexer #(.select(1), .width(2), .disabled("Z"), .enable("false")) multiplexer_6 (
    .in0(Stack_Pointer_q), .in1(adder_4_out), .out(multiplexer_6_out), .sel(URET));
  Adder #(.width(2)) adder_4 (.a(Stack_Pointer_q), .b(multiplexer_5_out), .out(adder_4_out));  // open: cin, cout
  Priority_Encoder #(.select(2), .disabled("Z")) priority_encoder_1 (
    .in0(1'b1), .in1(\中断按键参考电路_1_iror ), .in2(\中断按键参考电路_2_iror ), .in3(\中断按键参考电路_3_iror ),
    .out(priority_encoder_1_out));  // open: gs, en_out, en_in
  Multiplexer #(.select(2), .width(32), .disabled("Z"), .enable("false")) multiplexer_7 (
    .in1(32'h30ac), .in2(32'h3158), .in3(32'h3204), .out(multiplexer_7_out), .sel(IREncode));  // open: in0
  \单周期硬布线控制器  \u_单周期硬布线控制器_1  (
    .Funct({IR[30], IR[25], IR[14:12]}), .OP(IR[6:2]), .ALU_OP(\单周期硬布线控制器_1_alu_op ), .MemToReg(MTR),
    .MemWrite(MemWrite), .ALU_SRC(\单周期硬布线控制器_1_alu_src ), .RegWrite(RegWrite), .ecall(ecall), .S_type(SType),
    .Jalr(JALR), .Beq(\单周期硬布线控制器_1_beq ), .JAL(JAL), .Bne(\单周期硬布线控制器_1_bne ), .IR(IR[21]), .uret(URET),
    .Bge(Bge), .sb(sb), .ALT(ALT), .IRE(IRE), .IRD(IRD));  // open: RsUsed, RtUsed
  Multiplexer #(.select(1), .width(5), .disabled("Z"), .enable("false")) multiplexer_8 (
    .in0(IR[19:15]), .in1(5'b01010), .out(multiplexer_8_out), .sel(ecall));
  Multiplexer #(.select(1), .width(5), .disabled("Z"), .enable("false")) multiplexer_9 (
    .in0(IR[24:20]), .in1(5'b10001), .out(multiplexer_9_out), .sel(ecall));
  Multiplexer #(.select(1), .width(12), .disabled("Z"), .enable("false")) multiplexer_10 (
    .in0(IR[31:20]), .in1({IR[31:25], IR[11:7]}), .out(multiplexer_10_out), .sel(SType));
  assign bit_extender_1_out = {{8{IR[31]}}, {IR[31], IR[7], IR[30:25], IR[11:8]}};  // Bit_Extender bit_extender_1
  Multiplexer #(.select(1), .width(32), .disabled("Z"), .enable("false")) multiplexer_11 (
    .in0(multiplexer_7_out), .in1(mEPC_q), .out(IAddr), .sel(URET));
  D_Flip_Flop #(.trigger("high"), .Pre_Clr_Positions("LEGACY"), .NegatePresetClear("false"), .enable("true"), .NewFFLayout("false")) d_ff_1 (.Q(d_ff_1_q));  // open: clk, D, Qn, preset, en, reset
  // Probe on 13'h11
  Demultiplexer #(.select(2), .width(1), .tristate("false"), .disabled("Z"), .enable("false")) demultiplexer_1 (
    .out1(demultiplexer_1_out1), .out2(demultiplexer_1_out2), .out3(demultiplexer_1_out3), .in(URET),
    .sel(priority_encoder_1_out));  // open: out0
  assign bit_extender_2_out = {{20{multiplexer_10_out[11]}}, multiplexer_10_out};  // Bit_Extender bit_extender_2
  Multiplexer #(.select(1), .width(20), .disabled("Z"), .enable("false")) multiplexer_12 (
    .in0(bit_extender_1_out), .in1({IR[31], IR[19:12], IR[20], IR[30:21]}), .out(multiplexer_12_out),
    .sel(JAL));
  RAM #(.addrWidth(2), .dataWidth(32), .bus("separate"), .Select("low")) ram_1 (
    .addr(multiplexer_6_out), .din(mEPC_q), .data(mEPC_Ret), .str(IRespond), .clk(CLK), .ld(URET), .clr(RST));  // open: sel
  Comparator #(.width(13), .mode("twosComplement")) comparator_6 (
    .a(CNT_num), .b(13'h11), .eq(comparator_6_eq), .lt(comparator_6_lt));  // open: gt
  Clock #(.highDuration(1), .lowDuration(1)) clock_1 (.out(clock_1_out));
  Regifile regifile_1 (
    .Din(RDin), .Clk(CLK), .R1(regifile_1_r1), .R2(regifile_1_r2), .WE(RegWrite), .W_num(IR[11:7]),
    .R1_num(multiplexer_8_out), .R2_num(multiplexer_9_out));
  or or_10 (or_10_out, JALR, JAL);
  Counter #(.width(13), .max('h1fff), .ongoal("stay"), .trigger("rising"), .behavior("old")) counter_1 (
    .count(comparator_6_lt), .Q(CNT_num), .clk(clock_1_out));  // open: load, D, carry, clr, preset
  \中断按键参考电路  \u_中断按键参考电路_1  (
    .IRO(\中断按键参考电路_1_iro ), .\同步清零信号 (demultiplexer_1_out1), .IR(IR1_t), .IR_Light(W1), .CLK(CLK),
    .IROI(\中断按键参考电路_1_iroi ), .IROI_CLR(demultiplexer_2_out1), .IROR(\中断按键参考电路_1_iror ));
  \中断按键参考电路  \u_中断按键参考电路_2  (
    .IRO(\中断按键参考电路_2_iro ), .\同步清零信号 (demultiplexer_1_out2), .IR(IR2_t), .IR_Light(W2), .CLK(CLK),
    .IROI(\中断按键参考电路_2_iroi ), .IROI_CLR(demultiplexer_2_out2), .IROR(\中断按键参考电路_2_iror ));
  \中断按键参考电路  \u_中断按键参考电路_3  (
    .IRO(\中断按键参考电路_3_iro ), .\同步清零信号 (demultiplexer_1_out3), .IR(IR3_t), .IR_Light(W3), .CLK(CLK),
    .IROI(\中断按键参考电路_3_iroi ), .IROI_CLR(demultiplexer_2_out3), .IROR(\中断按键参考电路_3_iror ));
  Multiplexer #(.select(1), .width(32), .disabled("Z"), .enable("false")) multiplexer_13 (
    .in0(regifile_1_r2), .in1(bit_extender_2_out), .out(multiplexer_13_out), .sel(\单周期硬布线控制器_1_alu_src ));
  Multiplexer #(.select(1), .width(32), .disabled("Z"), .enable("false")) multiplexer_14 (
    .in0(multiplexer_18_out), .in1(adder_3_out), .out(RDin), .sel(or_10_out));
  nand nand_1 (nand_1_out, d_ff_1_q, comparator_6_eq);
  ALU alu_1 (
    .X(regifile_1_r1), .Y(multiplexer_13_out), .AluOP(\单周期硬布线控制器_1_alu_op ), .Equal(alu_1_equal),
    .Result(alu_1_result), .Result_2(alu_1_result_2), .out_4(alu_1_out_4));  // open: out_6
  Shifter #(.width(20), .shift("ll")) shifter_1 (.in(multiplexer_12_out), .\dist (5'b00001), .out(shifter_1_out));
  assign CLK = nand_1_out ? clock_1_out : 1'bz;  // Controlled_Buffer controlled_buffer_1
  Pull_Resistor #(.pull(1)) pull_resistor_4 (.node(CLK));
  Priority_Encoder #(.select(2), .disabled("Z")) priority_encoder_2 (
    .in0(1'b1), .in1(\中断按键参考电路_1_iro ), .in2(\中断按键参考电路_2_iro ), .in3(\中断按键参考电路_3_iro ), .out(IREncode));  // open: gs, en_out, en_in
  not not_4 (not_4_out, alu_1_equal);
  Multiplexer #(.select(2), .width(5), .disabled("Z"), .enable("false")) multiplexer_15 (
    .in0({5{1'b0}}), .in1(5'b01000), .in2(5'b10000), .in3(5'b11000), .out(multiplexer_15_out),
    .sel(alu_1_result[1:0]));
  assign PCOffset = {{12{shifter_1_out[19]}}, shifter_1_out};  // Bit_Extender bit_extender_3
  Demultiplexer #(.select(2), .width(1), .tristate("false"), .disabled(0), .enable("false")) demultiplexer_2 (
    .out1(demultiplexer_2_out1), .out2(demultiplexer_2_out2), .out3(demultiplexer_2_out3), .in(IE),
    .sel(IREncode));  // open: out0
  and and_2 (and_2_out, alu_1_out_4, Bge);
  and and_3 (and_3_out, \单周期硬布线控制器_1_bne , not_4_out);
  and and_4 (and_4_out, ecall, comparator_7_eq);
  Comparator #(.width(32), .mode("twosComplement")) comparator_7 (
    .a(regifile_1_r2), .b(32'h22), .eq(comparator_7_eq));  // open: gt, lt
  not not_5 (not_5_out, comparator_7_eq);
  Shifter #(.width(32), .shift("ll")) shifter_2 (.in(regifile_1_r2), .\dist (multiplexer_15_out), .out(MDin));
  or or_11 (or_11_out, \中断按键参考电路_1_iroi , \中断按键参考电路_2_iroi , \中断按键参考电路_3_iroi );
  and and_5 (and_5_out, \单周期硬布线控制器_1_beq , alu_1_equal);
  Register #(.width(32), .trigger("rising"), .Select("low")) LED_Register (
    .D(regifile_1_r1), .en(and_4_out), .Q(LedData), .clk(CLK), .clr(RST));
  and and_6 (go_halt, ecall, not_5_out);
  Multiplexer #(.select(1), .width(32), .disabled("Z"), .enable("false")) multiplexer_16 (
    .in0(alu_1_result), .in1(alu_1_result_2), .out(ALUO), .sel(ALT));
  and and_7 (IRespond, or_11_out, IE);
  or or_12 (PCSrc, and_3_out, and_5_out, and_2_out, JAL, JALR);
  Shifter #(.width(4), .shift("ll")) shifter_3 (.in(4'b0001), .\dist (alu_1_result[1:0]), .out(shifter_3_out));
  Multiplexer #(.select(1), .width(4), .disabled("Z"), .enable("false")) multiplexer_17 (
    .in0(4'b1111), .in1(shifter_3_out), .out(MemSel), .sel(sb));
  not not_6 (not_6_out, IRespond);
  or or_13 (or_13_out, IRD, IRespond, URET, IRE);
  and and_8 (and_8_out, ~IRD, not_6_out);  // AND_Gate
  Comparator #(.width(16), .mode("twosComplement")) comparator_8 (
    .a(\总周期数 ), .b({16{1'b0}}), .eq(comparator_8_eq));  // open: gt, lt
  Bit_Extender #(.in_width(30), .out_width(20), .\type ("zero")) bit_extender_4 (
    .in(alu_1_result[31:2]), .out(bit_extender_4_out));
  or or_14 (or_14_out, IRE, and_8_out);
  Register #(.width(1), .trigger("rising"), .Select("low")) u_IE (
    .D(or_14_out), .en(or_13_out), .Q(IE), .clk(CLK), .preset(comparator_8_eq));  // open: clr, cs
  // MIPS_RAM mips_ram_1: pin names not known; wires that end beside it: bit_extender_4_out, MDin, MemWrite, MemSel, CLK, RST, mips_ram_1_p7
  Multiplexer #(.select(1), .width(32), .disabled("Z"), .enable("false")) multiplexer_18 (
    .in0(ALUO), .in1(mips_ram_1_p7), .out(multiplexer_18_out), .sel(MTR));

  // Notes on the sheet:
  //   中断源
  //   中断等待指示
  //   总复位信号应将除ROM以外所有存储组件全部清零
  //   多级中断测试信号模拟器
  //   数码管输出
  //   数码管输出应该用寄存器锁存，否则显示数据只能一闪而过
  //   指令存储器
  //   contents of rom_1 (hex, n*v repeats v):
  //   7d000113 100413 1f41993 41f9d993 433 c00913 800b13 140413 f47413 800293 100313 499993 89e9b3 1300533
  //   2200893 73 406282b3 fe0294e3 140413 f00f93 1f47433 1c41413 800293 100313 49d993 89e9b3 1300533
  //   2200893 73 406282b3 fe0294e3 1c45413 406b0b33 b0463 f95ff06f 2b3 fff2c293 1029293 fff2e293 500533
  //   2200893 73 f5dff06f 1112023 410113 a12023 410113 812023 410113 1312023 410113 1412023 410113 1512023
  //   410113 1612023 410113 40e073 100b13 300a13 100a93 1600433 441413 14469b3 1300533 2200893 73 fe0416e3
  //   415a0a33 fe0a10e3 40f073 ffc10113 12b03 ffc10113 12a83 ffc10113 12a03 ffc10113 12983 ffc10113 12403
  //   ffc10113 12503 ffc10113 12883 200073 1112023 410113 a12023 410113 812023 410113 1312023 410113
  //   1412023 410113 1512023 410113 1612023 410113 40e073 200b13 300a13 100a93 1600433 441413 14469b3
  //   1300533 2200893 73 fe0416e3 415a0a33 fe0a10e3 40f073 ffc10113 12b03 ffc10113 12a83 ffc10113 12a03
  //   ffc10113 12983 ffc10113 12403 ffc10113 12503 ffc10113 12883 200073 1112023 410113 a12023 410113
  //   812023 410113 1312023 410113 1412023 410113 1512023 410113 1612023 410113 40e073 300b13 300a13
  //   100a93 1600433 441413 14469b3 1300533 2200893 73 fe0416e3 415a0a33 fe0a10e3 40f073 ffc10113 12b03
  //   ffc10113 12a83 ffc10113 12a03 ffc10113 12983 ffc10113 12403 ffc10113 12503 ffc10113 12883 200073
  //   为方便自动评测，需要输出PC，IR，寄存器堆写如数据RDin
  //   指令探针
  //   RAM写使能MemWrite、RAM写入数据MDin等信号
  //   指令字
  //   JAL
  //   JALR
  //   URET
  //   Bge
  //   BEQ offset
  //   JAL offset
  //   Beq
  //   Bne
  //   MemToReg
  //   MemWrite
  //   AluOP
  //   AluSrcB
  //   RegWrite
  //   S_Type
  //   ecall
  //   rd
  //   控制位
  //   暂停节拍，不能为0
  //   戳工具置1进入计数暂停模式，ctrl+k时钟自动运行到对应节拍暂停
  //   ctrl+k关闭时钟连续运行，将控制位置零，进入单步调试模式调试
  //   可计数暂停的时钟源
  //   Bne Judge
  //   Beq Judge
  //   Bge Judge
endmodule

module \封装正确性测试  (
);

  wire IR1, IR2, IR3, MemW, RegW;
  wire [31:0] IR, LED, MDin, PC, RDin;

  \单周期_多级中断  \u_单周期_多级中断_1  (
    .IR1(IR1), .IR2(IR2), .IR3(IR3), .RegWrite(RegW), .MemWrite(MemW), .PC(PC), .IR(IR), .RDin(RDin),
    .MDin(MDin), .LedData(LED));

  // Notes on the sheet:
  //   请检查上面封装有无位宽不匹配，引脚标签是否和连接的标签相对应，否则无法在educoder平台上正确测试
  //   单周期+多级中断封装测试
endmodule

module Flow_Register (
  input  [1:0] INForA,
  input  [1:0] INcor,
  input  [4:0] INrd,
  input  [31:0] IN4,
  input  [31:0] IN3,
  input  [31:0] IN2,
  input  [31:0] PC2,
  input  [31:0] PC,
  input  [31:0] IN1,
  input  CLK,
  input  RST,
  input  Flush,
  input  EN,
  output [1:0] OUTForA,
  output [1:0] OUTcor,
  output [4:0] OUTrd,
  output [31:0] OUT4,
  output [31:0] OUT3,
  output [31:0] OUT2,
  output [31:0] PC2_2,
  output [31:0] PC_2,
  output [31:0] OUT1
);

  wire [1:0] multiplexer_1_out, multiplexer_2_out;
  wire [4:0] multiplexer_3_out;
  wire [31:0] multiplexer_4_out, multiplexer_5_out, multiplexer_6_out, multiplexer_7_out, multiplexer_8_out,
       multiplexer_9_out;

  Multiplexer #(.select(1), .width(2), .disabled("Z"), .enable("false")) multiplexer_1 (
    .in0(INForA), .in1(2'b00), .out(multiplexer_1_out), .sel(Flush));
  Multiplexer #(.select(1), .width(2), .disabled("Z"), .enable("false")) multiplexer_2 (
    .in0(INcor), .in1(2'b00), .out(multiplexer_2_out), .sel(Flush));
  Multiplexer #(.select(1), .width(5), .disabled("Z"), .enable("false")) multiplexer_3 (
    .in0(INrd), .in1({5{1'b0}}), .out(multiplexer_3_out), .sel(Flush));
  Multiplexer #(.select(1), .width(32), .disabled("Z"), .enable("false")) multiplexer_4 (
    .in0(IN4), .in1({32{1'b0}}), .out(multiplexer_4_out), .sel(Flush));
  Multiplexer #(.select(1), .width(32), .disabled("Z"), .enable("false")) multiplexer_5 (
    .in0(IN3), .in1({32{1'b0}}), .out(multiplexer_5_out), .sel(Flush));
  Multiplexer #(.select(1), .width(32), .disabled("Z"), .enable("false")) multiplexer_6 (
    .in0(IN2), .in1({32{1'b0}}), .out(multiplexer_6_out), .sel(Flush));
  Multiplexer #(.select(1), .width(32), .disabled("Z"), .enable("false")) multiplexer_7 (
    .in0(PC2), .in1({32{1'b0}}), .out(multiplexer_7_out), .sel(Flush));
  Multiplexer #(.select(1), .width(32), .disabled("Z"), .enable("false")) multiplexer_8 (
    .in0(PC), .in1({32{1'b0}}), .out(multiplexer_8_out), .sel(Flush));
  Multiplexer #(.select(1), .width(32), .disabled("Z"), .enable("false")) multiplexer_9 (
    .in0(IN1), .in1({32{1'b0}}), .out(multiplexer_9_out), .sel(Flush));
  Register #(.width(2), .trigger("rising"), .Select("low")) register_1 (
    .D(multiplexer_1_out), .en(EN), .Q(OUTForA), .clk(CLK), .clr(RST));
  Register #(.width(2), .trigger("rising"), .Select("low")) register_2 (
    .D(multiplexer_2_out), .en(EN), .Q(OUTcor), .clk(CLK), .clr(RST));
  Register #(.width(5), .trigger("rising"), .Select("low")) register_3 (
    .D(multiplexer_3_out), .en(EN), .Q(OUTrd), .clk(CLK), .clr(RST));
  Register #(.width(32), .trigger("rising"), .Select("low")) register_4 (
    .D(multiplexer_4_out), .en(EN), .Q(OUT4), .clk(CLK), .clr(RST));
  Register #(.width(32), .trigger("rising"), .Select("low")) register_5 (
    .D(multiplexer_5_out), .en(EN), .Q(OUT3), .clk(CLK), .clr(RST));
  Register #(.width(32), .trigger("rising"), .Select("low")) register_6 (
    .D(multiplexer_6_out), .en(EN), .Q(OUT2), .clk(CLK), .clr(RST));
  Register #(.width(32), .trigger("rising"), .Select("low")) register_7 (
    .D(multiplexer_7_out), .en(EN), .Q(PC2_2), .clk(CLK), .clr(RST));
  Register #(.width(32), .trigger("rising"), .Select("low")) register_8 (
    .D(multiplexer_8_out), .en(EN), .Q(PC_2), .clk(CLK), .clr(RST));
  Register #(.width(32), .trigger("rising"), .Select("low")) register_9 (
    .D(multiplexer_9_out), .en(EN), .Q(OUT1), .clk(CLK), .clr(RST));
endmodule

module Flow_Register_Bit (
  input  [3:0] ALUOPIN,
  input  IN7,
  input  IN4,
  input  IN3,
  input  IN2,
  input  IN5,
  input  IN6,
  input  IN1,
  input  CLK,
  input  RST,
  input  Flush,
  input  EN,
  output [3:0] ALUOPOut,
  output OUT7,
  output OUT4,
  output OUT3,
  output OUT2,
  output OUT5,
  output OUT6,
  output OUT1
);

  wire multiplexer_2_out, multiplexer_3_out, multiplexer_4_out, multiplexer_5_out, multiplexer_6_out,
       multiplexer_7_out, multiplexer_8_out;
  wire [3:0] multiplexer_1_out;

  Multiplexer #(.select(1), .width(4), .disabled("Z"), .enable("false")) multiplexer_1 (
    .in0(ALUOPIN), .in1(4'b0000), .out(multiplexer_1_out), .sel(Flush));
  Multiplexer #(.select(1), .width(1), .disabled("Z"), .enable("false")) multiplexer_2 (
    .in0(IN7), .in1(1'b0), .out(multiplexer_2_out), .sel(Flush));
  Multiplexer #(.select(1), .width(1), .disabled("Z"), .enable("false")) multiplexer_3 (
    .in0(IN4), .in1(1'b0), .out(multiplexer_3_out), .sel(Flush));
  Multiplexer #(.select(1), .width(1), .disabled("Z"), .enable("false")) multiplexer_4 (
    .in0(IN3), .in1(1'b0), .out(multiplexer_4_out), .sel(Flush));
  Multiplexer #(.select(1), .width(1), .disabled("Z"), .enable("false")) multiplexer_5 (
    .in0(IN2), .in1(1'b0), .out(multiplexer_5_out), .sel(Flush));
  Multiplexer #(.select(1), .width(1), .disabled("Z"), .enable("false")) multiplexer_6 (
    .in0(IN5), .in1(1'b0), .out(multiplexer_6_out), .sel(Flush));
  Multiplexer #(.select(1), .width(1), .disabled("Z"), .enable("false")) multiplexer_7 (
    .in0(IN6), .in1(1'b0), .out(multiplexer_7_out), .sel(Flush));
  Multiplexer #(.select(1), .width(1), .disabled("Z"), .enable("false")) multiplexer_8 (
    .in0(IN1), .in1(1'b0), .out(multiplexer_8_out), .sel(Flush));
  Register #(.width(4), .trigger("rising"), .Select("low")) register_1 (
    .D(multiplexer_1_out), .en(EN), .Q(ALUOPOut), .clk(CLK), .clr(RST));
  Register #(.width(1), .trigger("rising"), .Select("low")) register_2 (
    .D(multiplexer_2_out), .en(EN), .Q(OUT7), .clk(CLK), .clr(RST));
  Register #(.width(1), .trigger("rising"), .Select("low")) register_3 (
    .D(multiplexer_3_out), .en(EN), .Q(OUT4), .clk(CLK), .clr(RST));
  Register #(.width(1), .trigger("rising"), .Select("low")) register_4 (
    .D(multiplexer_4_out), .en(EN), .Q(OUT3), .clk(CLK), .clr(RST));
  Register #(.width(1), .trigger("rising"), .Select("low")) register_5 (
    .D(multiplexer_5_out), .en(EN), .Q(OUT2), .clk(CLK), .clr(RST));
  Register #(.width(1), .trigger("rising"), .Select("low")) register_6 (
    .D(multiplexer_6_out), .en(EN), .Q(OUT5), .clk(CLK), .clr(RST));
  Register #(.width(1), .trigger("rising"), .Select("low")) register_7 (
    .D(multiplexer_7_out), .en(EN), .Q(OUT6), .clk(CLK), .clr(RST));
  Register #(.width(1), .trigger("rising"), .Select("low")) register_8 (
    .D(multiplexer_8_out), .en(EN), .Q(OUT1), .clk(CLK), .clr(RST));
endmodule

module Fowarding_Logic (
  input  Ex_MemRead,
  input  PCSrc,
  input  RsUsed,
  input  RtUsed,
  input  [4:0] Rs,
  input  Ex_RegWrite,
  input  [4:0] Rt,
  input  MEM_RegWrite,
  input  [4:0] ExAddr,
  input  [4:0] MEMAddr,
  output Stall,
  output Flush,
  output [1:0] RsForward,
  output [1:0] RtForward
);

  wire and_1_out, and_2_out, and_3_out, and_4_out, and_5_out, and_6_out, comparator_1_eq, comparator_2_eq,
       comparator_3_eq, comparator_4_eq, comparator_5_eq, comparator_6_eq, loaduse_1_datahazzard, not_1_out,
       not_2_out;
  wire [1:0] and_7_out, and_9_out;

  Comparator #(.width(5), .mode("unsigned")) comparator_1 (
    .a(Rs), .b({5{1'b0}}), .eq(comparator_1_eq));  // open: gt, lt
  not not_1 (not_1_out, comparator_1_eq);
  not not_2 (not_2_out, comparator_2_eq);
  Comparator #(.width(5), .mode("unsigned")) comparator_2 (
    .a(Rt), .b({5{1'b0}}), .eq(comparator_2_eq));  // open: gt, lt
  Comparator #(.width(5), .mode("unsigned")) comparator_3 (.a(Rs), .b(ExAddr), .eq(comparator_3_eq));  // open: gt, lt
  Comparator #(.width(5), .mode("unsigned")) comparator_4 (.a(Rt), .b(MEMAddr), .eq(comparator_4_eq));  // open: gt, lt
  Comparator #(.width(5), .mode("unsigned")) comparator_5 (.a(Rs), .b(MEMAddr), .eq(comparator_5_eq));  // open: gt, lt
  Comparator #(.width(5), .mode("unsigned")) comparator_6 (.a(Rt), .b(ExAddr), .eq(comparator_6_eq));  // open: gt, lt
  LoadUse loaduse_1 (
    .RsUsed(RsUsed), .RtUsed(RtUsed), .Rsnz(not_1_out), .Rtnz(not_2_out), .Rseq(comparator_3_eq),
    .Rteq(comparator_6_eq), .ExMemRead(Ex_MemRead), .DataHazzard(loaduse_1_datahazzard));
  and and_1 (and_1_out, RsUsed, not_1_out);
  and and_2 (and_2_out, Ex_RegWrite, comparator_3_eq);
  and and_3 (and_3_out, MEM_RegWrite, comparator_5_eq);
  and and_4 (and_4_out, RtUsed, not_2_out);
  and and_5 (and_5_out, Ex_RegWrite, comparator_6_eq);
  and and_6 (and_6_out, MEM_RegWrite, comparator_4_eq);
  not not_3 (Stall, loaduse_1_datahazzard);
  and and_7 (and_7_out[0], and_1_out, and_2_out);
  and and_8 (and_7_out[1], and_1_out, and_3_out);
  and and_9 (and_9_out[0], and_4_out, and_5_out);
  and and_10 (and_9_out[1], and_4_out, and_6_out);
  or or_1 (Flush, PCSrc, loaduse_1_datahazzard);
  Multiplexer #(.select(2), .width(2), .disabled("Z"), .enable("false")) multiplexer_1 (
    .in0(2'b00), .in1(2'b10), .in2(2'b01), .in3(2'b10), .out(RsForward), .sel(and_7_out));
  Multiplexer #(.select(2), .width(2), .disabled("Z"), .enable("false")) multiplexer_2 (
    .in0(2'b00), .in1(2'b10), .in2(2'b01), .in3(2'b10), .out(RtForward), .sel(and_9_out));

  // Notes on the sheet:
  //   LoadUse
endmodule

module LoadUse (
  input  RsUsed,
  input  RtUsed,
  input  Rsnz,
  input  Rtnz,
  input  Rseq,
  input  Rteq,
  input  ExMemRead,
  output DataHazzard
);

  wire and_1_out, and_2_out;

  and and_1 (and_1_out, RsUsed, Rsnz, ExMemRead, Rseq);
  and and_2 (and_2_out, RtUsed, Rtnz, ExMemRead, Rteq);
  or or_1 (DataHazzard, and_1_out, and_2_out);
endmodule
